// Logisim project CPU8.circ as structural Verilog: 16 circuits, main circuit BOARD
module BOARD (
);

  wire and_1_out, and_2_out, and_3_out, and_4_out, and_5_out, and_6_out, and_7_out, and_8_out, and_9_out,
       and_10_out, and_11_out, and_12_out, and_13_out, and_14_out, and_15_out, and_16_out, and_17_out,
       and_18_out, and_19_out, and_20_out, and_21_out, and_22_out, and_23_out, and_24_out, and_25_out,
       and_26_out, and_27_out, and_28_out, and_29_out, and_30_out, and_31_out, and_32_out, and_33_out,
       and_34_out, and_35_out, and_36_out, and_37_out, and_38_out, and_39_out, and_40_out, and_41_out,
       and_42_out, and_43_out, and_44_out, and_45_out, and_46_out, and_47_out, and_48_out, and_49_out,
       and_50_out, and_51_out, and_52_out, and_53_out, and_54_out, and_55_out, and_56_out, and_57_out,
       and_58_out, and_59_out, and_60_out, and_61_out, and_62_out, and_63_out, and_64_out, and_65_out,
       and_66_out, and_67_out, and_68_out, and_69_out, and_70_out, and_71_out, and_72_out, and_73_out,
       and_74_out, and_75_out, and_76_out, and_77_out, and_78_out, and_79_out, and_80_out, and_81_out,
       and_82_out, and_83_out, and_84_out, and_85_out, and_86_out, and_87_out, and_88_out, and_89_out,
       and_90_out, and_91_out, and_92_out, and_93_out, and_94_out, and_95_out, and_96_out, and_97_out,
       and_98_out, and_99_out, and_100_out, CLOCK_out, controlled_buffer_11_out, dec4_1__0_2, dec4_1__1_2,
       dec4_1__2_2, dec4_1__3_2, dec4_1__4, dec4_1__5, dec4_1__6, dec4_1__7, dec4_1__8, dec4_1__9, dec4_1_a,
       dec4_1_b, dec4_1_c, dec4_1_d, dec4_1_e_2, dec4_1_f, decoder_1_out0, decoder_1_out1, decoder_1_out2,
       decoder_1_out3, decoder_2_out0, decoder_2_out1, decoder_2_out2, decoder_2_out3, decoder_2_out4,
       decoder_2_out5, decoder_2_out6, decoder_2_out7, not_1_out, not_2_out, not_3_out, or_1_out, or_2_out,
       or_3_out, or_4_out, or_5_out, or_6_out, or_7_out, or_8_out, or_9_out, or_10_out, or_11_out, or_12_out,
       or_13_out, or_14_out, or_15_out, or_16_out, or_17_out, or_18_out, or_19_out, or_20_out, or_21_out,
       or_22_out, or_23_out, or_24_out, or_25_out, or_26_out, or_27_out, pull_resistor_1_node, RESET_out,
       toggle_1_q, toggle_2_q, toggle_3_q, toggle_4_q, toggle_5_q;
  wire [0:0] controlled_buffer_9_out, controlled_buffer_9_out_2, controlled_buffer_10_out,
       controlled_buffer_10_out_2, controlled_buffer_15_out, controlled_buffer_40_out;
  wire [1:0] controlled_buffer_13_out, controlled_buffer_16_out, controlled_buffer_21_out,
       controlled_buffer_45_out, controlled_buffer_106_out, counter2_1_q, counter2_2_q, F_q, F_q_2, F_q_3,
       F_q_4;
  wire [1:1] controlled_buffer_38_out, controlled_buffer_39_out, controlled_buffer_123_out,
       controlled_buffer_124_out;
  wire [2:0] controlled_buffer_13_out_3, controlled_buffer_14_out, controlled_buffer_17_out,
       controlled_buffer_22_out, controlled_buffer_23_out, controlled_buffer_42_out,
       controlled_buffer_113_out, pull_resistor_3_node;
  wire [3:0] alu_1_c, controlled_buffer_10_out_3;
  wire [3:2] controlled_buffer_20_out;
  wire [5:0] controlled_buffer_13_out_2;
  wire [7:0] A_2_q, alu_1_r, controlled_buffer_112_out, controlled_buffer_121_out, controlled_buffer_133_out,
       demultiplexer_1_out0, demultiplexer_1_out1, demultiplexer_1_out2, demultiplexer_1_out3,
       demultiplexer_1_out4, demultiplexer_1_out5, demultiplexer_1_out6, demultiplexer_1_out7,
       multiplexer_1_out, multiplexer_2_out, multiplexer_3_out, multiplexer_4_out, multiplexer_5_out,
       multiplexer_6_out, multiplexer_7_out, multiplexer_8_out, multiplexer_9_out, multiplexer_10_out,
       multiplexer_11_out, P_q, R_2_q, ram16_1_out, S_q, W_q, X_q, Y_q, Z_q;

  TOGGLE toggle_1 (.C(pull_resistor_1_node), .R(RESET_out), .T(1'b1), .D(1'b0), .Q(toggle_1_q), .W(1'b0));
  Pull_Resistor pull_resistor_1 (.node(pull_resistor_1_node));
  Pull_Resistor pull_resistor_2 (.node(pull_resistor_3_node[1]));
  assign pull_resistor_1_node = and_5_out ? 1'b1 : 1'bz;  // Controlled_Buffer controlled_buffer_1
  not not_1 (not_1_out, or_10_out);
  or or_1 (or_1_out, and_6_out, and_7_out);
  assign pull_resistor_1_node = or_1_out ? 1'b1 : 1'bz;  // Controlled_Buffer controlled_buffer_2
  and and_1 (and_1_out, and_100_out, ~and_61_out);  // AND_Gate
  assign pull_resistor_1_node = and_9_out ? 1'b1 : 1'bz;  // Controlled_Buffer controlled_buffer_3
  Decoder #(.select(2), .disabled(0)) decoder_1 (
    .out0(decoder_1_out0), .out1(decoder_1_out1), .out2(decoder_1_out2), .out3(decoder_1_out3),
    .sel(controlled_buffer_16_out), .en(pull_resistor_3_node[1]));
  and and_2 (and_2_out, and_100_out, or_6_out);
  assign pull_resistor_1_node = and_2_out ? 1'b1 : 1'bz;  // Controlled_Buffer controlled_buffer_4
  assign pull_resistor_1_node = and_12_out ? 1'b1 : 1'bz;  // Controlled_Buffer controlled_buffer_5
  assign pull_resistor_1_node = and_14_out ? 1'b1 : 1'bz;  // Controlled_Buffer controlled_buffer_6
  and and_3 (and_3_out, and_100_out, or_8_out);
  assign pull_resistor_1_node = and_3_out ? 1'b1 : 1'bz;  // Controlled_Buffer controlled_buffer_7
  and and_4 (and_4_out, and_100_out, or_9_out);
  assign pull_resistor_1_node = and_4_out ? 1'b1 : 1'bz;  // Controlled_Buffer controlled_buffer_8
  and and_5 (and_5_out, and_26_out, and_100_out);
  COUNTER2 counter2_1 (.I(not_1_out), .D(2'b00), .W(or_10_out), .C(and_8_out), .R(RESET_out), .Q(counter2_1_q));
  and and_6 (and_6_out, or_10_out, toggle_1_q, and_1_out);
  and and_7 (and_7_out, ~counter2_1_q[0], ~counter2_1_q[1], and_16_out, and_1_out);  // AND_Gate
  and and_8 (and_8_out, and_1_out, or_2_out);
  or or_2 (or_2_out, or_12_out, and_16_out);
  TOGGLE toggle_2 (.C(and_9_out), .R(RESET_out), .T(1'b1), .D(1'b0), .Q(toggle_2_q), .W(1'b0));
  and and_9 (and_9_out, and_100_out, or_3_out);
  or or_3 (or_3_out, toggle_2_q, and_30_out);
  and and_10 (and_10_out, controlled_buffer_23_out[2], controlled_buffer_23_out[1], controlled_buffer_23_out[0]);
  and and_11 (and_11_out, ~decoder_1_out3, and_10_out);  // AND_Gate
  or or_4 (or_4_out, decoder_1_out3, and_10_out);
  or or_5 (or_5_out, or_4_out, and_62_out);
  TOGGLE toggle_3 (.C(and_2_out), .R(RESET_out), .T(1'b1), .D(1'b0), .Q(toggle_3_q), .W(1'b0));
  or or_6 (or_6_out, and_54_out, and_51_out, and_34_out);
  COUNTER2 counter2_2 (.I(1'b1), .D(2'b00), .W(1'b0), .C(and_13_out), .R(RESET_out), .Q(counter2_2_q));
  // Probe on counter2_2_q
  and and_12 (and_12_out, ~counter2_2_q[0], ~counter2_2_q[1], and_46_out, and_100_out);  // AND_Gate
  and and_13 (and_13_out, and_100_out, or_7_out);
  or or_7 (or_7_out, or_11_out, and_46_out);
  and and_14 (and_14_out, and_100_out, and_38_out);
  TOGGLE toggle_4 (.C(and_3_out), .R(RESET_out), .T(1'b1), .D(1'b0), .Q(toggle_4_q), .W(1'b0));
  or or_8 (or_8_out, and_39_out, toggle_4_q);
  assign {controlled_buffer_42_out[2], controlled_buffer_9_out_2[0], controlled_buffer_42_out[0], controlled_buffer_9_out[0]} = toggle_4_q ? 4'b0000 : 4'bz;  // Controlled_Buffer controlled_buffer_9
  assign {controlled_buffer_10_out_3[3], controlled_buffer_10_out_2[0], pull_resistor_3_node[2], controlled_buffer_10_out[0]} = toggle_4_q ? 4'b1111 : 4'bz;  // Controlled_Buffer controlled_buffer_10
  TOGGLE toggle_5 (.C(and_4_out), .R(RESET_out), .T(1'b1), .D(1'b0), .Q(toggle_5_q), .W(1'b0));
  or or_9 (or_9_out, or_15_out, toggle_5_q);
  and and_15 (and_15_out, ~RESET_out, ~toggle_1_q, controlled_buffer_13_out[1], controlled_buffer_13_out[0], ~controlled_buffer_13_out_2[5], ~controlled_buffer_13_out_3[2], controlled_buffer_13_out_3[1], controlled_buffer_13_out_3[0], controlled_buffer_13_out_2[1], controlled_buffer_13_out_2[0]);  // AND_Gate
  assign controlled_buffer_11_out = and_15_out ? 1'b1 : 1'bz;  // Controlled_Buffer controlled_buffer_11
  or or_10 (or_10_out, and_42_out, and_47_out, and_59_out, and_58_out);
  // Probe on counter2_1_q
  and and_16 (and_16_out, ~counter2_1_q[0], ~counter2_1_q[1], ~toggle_1_q, ~controlled_buffer_13_out_2[1], controlled_buffer_13_out_2[0]);  // AND_Gate
  assign {pull_resistor_3_node[1], controlled_buffer_113_out[2]} = and_18_out ? 2'b11 : 2'bz;  // Controlled_Buffer controlled_buffer_12
  and and_17 (and_17_out, F_q_4[1], toggle_2_q);
  and and_18 (and_18_out, ~F_q_4[1], toggle_2_q);  // AND_Gate
  and and_19 (and_19_out, decoder_1_out3, pull_resistor_3_node[0]);
  assign {controlled_buffer_13_out, controlled_buffer_13_out_2[5], controlled_buffer_13_out_3, controlled_buffer_13_out_2[1:0]} = and_19_out ? Z_q : 8'bz;  // Controlled_Buffer controlled_buffer_13
  Multiplexer #(.width(8), .enable("false")) multiplexer_1 (
    .in0({controlled_buffer_13_out, controlled_buffer_13_out_2[5], controlled_buffer_13_out_3, controlled_buffer_13_out_2[1:0]}),
    .in1(demultiplexer_1_out7), .out(multiplexer_1_out), .sel(and_11_out));
  Multiplexer #(.width(8), .enable("false")) multiplexer_2 (
    .in0(multiplexer_1_out), .in1(demultiplexer_1_out3), .out(multiplexer_2_out), .sel(and_62_out));
  // Probe on Z_q
  REG8 Z (.C(and_20_out), ._0(RESET_out), .D(multiplexer_2_out), .Q(Z_q));
  and and_20 (and_20_out, or_5_out, and_100_out);
  and and_21 (and_21_out, ~F_q[0], F_q[1], toggle_3_q);  // AND_Gate
  and and_22 (and_22_out, ~toggle_3_q, ~toggle_1_q, controlled_buffer_13_out_2[1], ~controlled_buffer_13_out_2[0]);  // AND_Gate
  or or_11 (or_11_out, counter2_2_q[0], counter2_2_q[1]);
  and and_23 (and_23_out, ~controlled_buffer_13_out_2[0], controlled_buffer_13_out_2[1], ~toggle_1_q, ~toggle_4_q);  // AND_Gate
  assign controlled_buffer_14_out = toggle_4_q ? 3'b011 : 3'bz;  // Controlled_Buffer controlled_buffer_14
  and and_24 (and_24_out, controlled_buffer_13_out_2[0], controlled_buffer_13_out_2[1], ~toggle_1_q, ~toggle_5_q);  // AND_Gate
  and and_25 (and_25_out, toggle_5_q, ~F_q_3[1], F_q_3[0]);  // AND_Gate
  and and_26 (and_26_out, ~counter2_1_q[0], counter2_1_q[1]);  // AND_Gate
  and and_27 (and_27_out, and_26_out, ~F_q_3[1], F_q_3[0]);  // AND_Gate
  and and_28 (and_28_out, F_q[0], ~F_q[1], counter2_1_q[0], ~counter2_1_q[1]);  // AND_Gate
  or or_12 (or_12_out, counter2_1_q[0], counter2_1_q[1]);
  and and_29 (and_29_out, and_16_out, ~controlled_buffer_13_out_3[1], ~controlled_buffer_13_out_3[0]);  // AND_Gate
  assign {controlled_buffer_10_out_3[3], controlled_buffer_42_out[0], controlled_buffer_42_out[2], controlled_buffer_15_out[0]} = and_18_out ? 4'b0000 : 4'bz;  // Controlled_Buffer controlled_buffer_15
  assign controlled_buffer_16_out = and_18_out ? F_q_2 : 2'bz;  // Controlled_Buffer controlled_buffer_16
  assign controlled_buffer_17_out = and_17_out ? 3'b100 : 3'bz;  // Controlled_Buffer controlled_buffer_17
  and and_30 (and_30_out, ~toggle_2_q, ~toggle_1_q, ~controlled_buffer_13_out_2[1], ~controlled_buffer_13_out_2[0]);  // AND_Gate
  assign {controlled_buffer_13_out, controlled_buffer_13_out_2[5], controlled_buffer_13_out_3, controlled_buffer_13_out_2[1:0]} = and_44_out ? Y_q : 8'bz;  // Controlled_Buffer controlled_buffer_18
  and and_31 (and_31_out, controlled_buffer_23_out[2], controlled_buffer_23_out[1], ~controlled_buffer_23_out[0]);  // AND_Gate
  or or_13 (or_13_out, decoder_1_out2, and_31_out);
  Multiplexer #(.width(8), .enable("false")) multiplexer_3 (
    .in0({controlled_buffer_13_out, controlled_buffer_13_out_2[5], controlled_buffer_13_out_3, controlled_buffer_13_out_2[1:0]}),
    .in1(demultiplexer_1_out6), .out(multiplexer_3_out), .sel(and_31_out));
  REG8 Y (.C(and_32_out), ._0(RESET_out), .D(multiplexer_3_out), .Q(Y_q));
  and and_32 (and_32_out, or_13_out, and_100_out);
  and and_33 (and_33_out, ~F_q_3[0], F_q_3[1], and_21_out);  // AND_Gate
  and and_34 (and_34_out, and_22_out, ~controlled_buffer_13_out_3[1], ~controlled_buffer_13_out_3[0]);  // AND_Gate
  and and_35 (and_35_out, ~F_q[0], F_q[1], counter2_2_q[0], ~counter2_2_q[1]);  // AND_Gate
  and and_36 (and_36_out, ~counter2_2_q[0], ~counter2_2_q[1], ~toggle_1_q, controlled_buffer_13_out_2[1], ~controlled_buffer_13_out_2[0]);  // AND_Gate
  assign {pull_resistor_3_node[2], controlled_buffer_10_out_3[3]} = and_37_out ? 2'b11 : 2'bz;  // Controlled_Buffer controlled_buffer_19
  and and_37 (and_37_out, ~F_q[0], F_q[1], ~counter2_2_q[0], counter2_2_q[1]);  // AND_Gate
  and and_38 (and_38_out, counter2_2_q[0], counter2_2_q[1]);
  assign {controlled_buffer_20_out, controlled_buffer_42_out[2], controlled_buffer_15_out[0]} = and_38_out ? 4'b0000 : 4'bz;  // Controlled_Buffer controlled_buffer_20
  assign {controlled_buffer_10_out_3[3], controlled_buffer_10_out_3[0], controlled_buffer_21_out} = and_39_out ? 4'b1111 : 4'bz;  // Controlled_Buffer controlled_buffer_21
  and and_39 (and_39_out, controlled_buffer_13_out_3[0], controlled_buffer_13_out_3[1], controlled_buffer_13_out_3[2], ~controlled_buffer_13_out_2[5], and_23_out);  // AND_Gate
  assign controlled_buffer_22_out = toggle_4_q ? 3'b000 : 3'bz;  // Controlled_Buffer controlled_buffer_22
  assign controlled_buffer_23_out = toggle_4_q ? 3'b011 : 3'bz;  // Controlled_Buffer controlled_buffer_23
  assign controlled_buffer_10_out_3[3] = and_41_out ? 1'b1 : 1'bz;  // Controlled_Buffer controlled_buffer_24
  assign controlled_buffer_42_out[2] = and_41_out ? 1'b0 : 1'bz;  // Controlled_Buffer controlled_buffer_25
  and and_40 (and_40_out, ~controlled_buffer_13_out_3[1], controlled_buffer_13_out_3[0], and_24_out);  // AND_Gate
  and and_41 (and_41_out, ~controlled_buffer_13_out_3[1], ~controlled_buffer_13_out_3[0], and_24_out);  // AND_Gate
  assign controlled_buffer_10_out_3[3] = and_25_out ? 1'b1 : 1'bz;  // Controlled_Buffer controlled_buffer_26
  assign controlled_buffer_22_out = and_25_out ? 3'b010 : 3'bz;  // Controlled_Buffer controlled_buffer_27
  assign {pull_resistor_3_node[1], pull_resistor_3_node[2]} = and_27_out ? 2'b11 : 2'bz;  // Controlled_Buffer controlled_buffer_28
  assign {controlled_buffer_42_out[0], controlled_buffer_42_out[2]} = and_27_out ? 2'b00 : 2'bz;  // Controlled_Buffer controlled_buffer_29
  assign {pull_resistor_3_node[1], controlled_buffer_113_out[2]} = and_42_out ? 2'b11 : 2'bz;  // Controlled_Buffer controlled_buffer_30
  and and_42 (and_42_out, ~F_q_3[0], ~F_q_3[1], and_28_out);  // AND_Gate
  assign {controlled_buffer_10_out_3[0], controlled_buffer_10_out_3[3]} = and_60_out ? 2'b11 : 2'bz;  // Controlled_Buffer controlled_buffer_31
  assign {controlled_buffer_10_out_3[0], controlled_buffer_10_out_3[3]} = and_61_out ? 2'b11 : 2'bz;  // Controlled_Buffer controlled_buffer_32
  assign controlled_buffer_10_out_3[3] = and_29_out ? 1'b1 : 1'bz;  // Controlled_Buffer controlled_buffer_33
  assign controlled_buffer_9_out_2[0] = and_29_out ? 1'b0 : 1'bz;  // Controlled_Buffer controlled_buffer_34
  assign {controlled_buffer_10_out_3[3], pull_resistor_3_node[1]} = and_17_out ? 2'b11 : 2'bz;  // Controlled_Buffer controlled_buffer_35
  and and_43 (and_43_out, and_30_out, ~controlled_buffer_13_out_2[5]);  // AND_Gate
  assign controlled_buffer_10_out_3[3] = and_43_out ? 1'b1 : 1'bz;  // Controlled_Buffer controlled_buffer_36
  and and_44 (and_44_out, decoder_1_out2, pull_resistor_3_node[0]);
  or or_14 (or_14_out, decoder_1_out1, and_49_out);
  // Probe on Y_q
  assign {controlled_buffer_42_out[0], controlled_buffer_42_out[2]} = and_33_out ? 2'b00 : 2'bz;  // Controlled_Buffer controlled_buffer_37
  assign {controlled_buffer_38_out[1], controlled_buffer_10_out_2[0]} = and_33_out ? 2'b11 : 2'bz;  // Controlled_Buffer controlled_buffer_38
  assign {controlled_buffer_42_out[0], controlled_buffer_39_out[1], controlled_buffer_9_out_2[0]} = and_45_out ? 3'b000 : 3'bz;  // Controlled_Buffer controlled_buffer_39
  assign {controlled_buffer_10_out_3[3], controlled_buffer_40_out[0]} = and_45_out ? 2'b11 : 2'bz;  // Controlled_Buffer controlled_buffer_40
  and and_45 (and_45_out, F_q_3[0], F_q_3[1], ~F_q_4[0], ~F_q_4[1], and_35_out);  // AND_Gate
  and and_46 (and_46_out, and_36_out, ~controlled_buffer_13_out_2[5], ~controlled_buffer_13_out_3[2], controlled_buffer_13_out_3[1], controlled_buffer_13_out_3[0]);  // AND_Gate
  assign controlled_buffer_9_out_2[0] = and_46_out ? 1'b0 : 1'bz;  // Controlled_Buffer controlled_buffer_41
  assign {controlled_buffer_42_out[1], controlled_buffer_9_out_2[0], controlled_buffer_42_out[0], controlled_buffer_42_out[2]} = and_37_out ? 4'b0000 : 4'bz;  // Controlled_Buffer controlled_buffer_42
  assign controlled_buffer_17_out = and_37_out ? 3'b110 : 3'bz;  // Controlled_Buffer controlled_buffer_43
  assign {controlled_buffer_10_out_2[0], controlled_buffer_113_out[2]} = and_38_out ? 2'b11 : 2'bz;  // Controlled_Buffer controlled_buffer_44
  assign {controlled_buffer_9_out_2[0], controlled_buffer_42_out[0], controlled_buffer_45_out} = and_39_out ? 4'b0000 : 4'bz;  // Controlled_Buffer controlled_buffer_45
  assign controlled_buffer_17_out = and_39_out ? 3'b011 : 3'bz;  // Controlled_Buffer controlled_buffer_46
  assign controlled_buffer_22_out = and_41_out ? 3'b010 : 3'bz;  // Controlled_Buffer controlled_buffer_47
  assign controlled_buffer_14_out = and_41_out ? {1'b0, controlled_buffer_13_out_2[5], controlled_buffer_13_out_3[2]} : 3'bz;  // Controlled_Buffer controlled_buffer_48
  assign controlled_buffer_17_out = and_41_out ? {1'b0, controlled_buffer_13_out} : 3'bz;  // Controlled_Buffer controlled_buffer_49
  or or_15 (or_15_out, and_40_out, and_41_out);
  assign controlled_buffer_14_out = and_25_out ? {1'b0, F_q_4} : 3'bz;  // Controlled_Buffer controlled_buffer_50
  assign controlled_buffer_17_out = and_25_out ? 3'b100 : 3'bz;  // Controlled_Buffer controlled_buffer_51
  assign controlled_buffer_16_out = and_27_out ? F_q_4 : 2'bz;  // Controlled_Buffer controlled_buffer_52
  assign {controlled_buffer_10_out_3[3], controlled_buffer_42_out[0], controlled_buffer_42_out[2], controlled_buffer_15_out[0]} = and_42_out ? 4'b0000 : 4'bz;  // Controlled_Buffer controlled_buffer_53
  assign controlled_buffer_16_out = and_42_out ? F_q_4 : 2'bz;  // Controlled_Buffer controlled_buffer_54
  and and_47 (and_47_out, F_q_3[0], F_q_3[1], ~F_q_2[0], ~F_q_2[1], and_28_out);  // AND_Gate
  assign controlled_buffer_14_out = and_60_out ? 3'b011 : 3'bz;  // Controlled_Buffer controlled_buffer_55
  assign controlled_buffer_23_out = and_60_out ? 3'b011 : 3'bz;  // Controlled_Buffer controlled_buffer_56
  assign controlled_buffer_14_out = and_61_out ? 3'b011 : 3'bz;  // Controlled_Buffer controlled_buffer_57
  assign controlled_buffer_14_out = and_29_out ? {1'b0, controlled_buffer_13_out} : 3'bz;  // Controlled_Buffer controlled_buffer_58
  assign controlled_buffer_23_out = and_17_out ? {1'b1, F_q_2} : 3'bz;  // Controlled_Buffer controlled_buffer_59
  assign controlled_buffer_16_out = and_17_out ? F_q_2 : 2'bz;  // Controlled_Buffer controlled_buffer_60
  assign controlled_buffer_22_out = and_43_out ? controlled_buffer_13_out_3 : 3'bz;  // Controlled_Buffer controlled_buffer_61
  and and_48 (and_48_out, decoder_1_out1, pull_resistor_3_node[0]);
  assign {controlled_buffer_13_out, controlled_buffer_13_out_2[5], controlled_buffer_13_out_3, controlled_buffer_13_out_2[1:0]} = and_48_out ? X_q : 8'bz;  // Controlled_Buffer controlled_buffer_62
  and and_49 (and_49_out, controlled_buffer_23_out[2], ~controlled_buffer_23_out[1], controlled_buffer_23_out[0]);  // AND_Gate
  Multiplexer #(.width(8), .enable("false")) multiplexer_4 (
    .in0({controlled_buffer_13_out, controlled_buffer_13_out_2[5], controlled_buffer_13_out_3, controlled_buffer_13_out_2[1:0]}),
    .in1(demultiplexer_1_out5), .out(multiplexer_4_out), .sel(and_49_out));
  // Probe on X_q
  REG8 X (.C(and_50_out), ._0(RESET_out), .D(multiplexer_4_out), .Q(X_q));
  and and_50 (and_50_out, or_14_out, and_100_out);
  and and_51 (and_51_out, and_22_out, controlled_buffer_13_out_3[1], ~controlled_buffer_13_out_3[0]);  // AND_Gate
  assign controlled_buffer_22_out = and_45_out ? 3'b001 : 3'bz;  // Controlled_Buffer controlled_buffer_63
  assign controlled_buffer_17_out = and_46_out ? 3'b111 : 3'bz;  // Controlled_Buffer controlled_buffer_64
  assign {controlled_buffer_10_out_3[3], pull_resistor_3_node[1], controlled_buffer_10_out_3[0]} = and_46_out ? 3'b111 : 3'bz;  // Controlled_Buffer controlled_buffer_65
  assign controlled_buffer_22_out = and_37_out ? 3'b001 : 3'bz;  // Controlled_Buffer controlled_buffer_66
  assign controlled_buffer_14_out = and_37_out ? 3'b101 : 3'bz;  // Controlled_Buffer controlled_buffer_67
  assign controlled_buffer_14_out = and_39_out ? 3'b101 : 3'bz;  // Controlled_Buffer controlled_buffer_68
  assign controlled_buffer_22_out = and_39_out ? 3'b001 : 3'bz;  // Controlled_Buffer controlled_buffer_69
  and and_52 (and_52_out, and_26_out, F_q_3[1], ~F_q_3[0]);  // AND_Gate
  assign controlled_buffer_17_out = and_60_out ? 3'b101 : 3'bz;  // Controlled_Buffer controlled_buffer_70
  assign controlled_buffer_22_out = and_60_out ? 3'b001 : 3'bz;  // Controlled_Buffer controlled_buffer_71
  assign controlled_buffer_23_out = and_61_out ? 3'b111 : 3'bz;  // Controlled_Buffer controlled_buffer_72
  assign controlled_buffer_22_out = and_61_out ? 3'b000 : 3'bz;  // Controlled_Buffer controlled_buffer_73
  assign controlled_buffer_17_out = and_29_out ? 3'b101 : 3'bz;  // Controlled_Buffer controlled_buffer_74
  assign controlled_buffer_22_out = and_29_out ? 3'b001 : 3'bz;  // Controlled_Buffer controlled_buffer_75
  assign controlled_buffer_14_out = and_17_out ? {1'b0, F_q_2} : 3'bz;  // Controlled_Buffer controlled_buffer_76
  assign controlled_buffer_22_out = and_17_out ? {F_q_4[0], F_q_3} : 3'bz;  // Controlled_Buffer controlled_buffer_77
  assign controlled_buffer_14_out = and_43_out ? {1'b0, controlled_buffer_13_out} : 3'bz;  // Controlled_Buffer controlled_buffer_78
  assign controlled_buffer_17_out = and_43_out ? 3'b000 : 3'bz;  // Controlled_Buffer controlled_buffer_79
  and and_53 (and_53_out, controlled_buffer_23_out[2], ~controlled_buffer_23_out[1], ~controlled_buffer_23_out[0]);  // AND_Gate
  or or_16 (or_16_out, decoder_1_out0, and_53_out);
  and and_54 (and_54_out, ~F_q_3[0], ~F_q_3[1], and_21_out);  // AND_Gate
  assign controlled_buffer_14_out = and_45_out ? 3'b101 : 3'bz;  // Controlled_Buffer controlled_buffer_80
  assign controlled_buffer_17_out = and_45_out ? 3'b100 : 3'bz;  // Controlled_Buffer controlled_buffer_81
  assign controlled_buffer_14_out = and_46_out ? 3'b011 : 3'bz;  // Controlled_Buffer controlled_buffer_82
  assign controlled_buffer_22_out = and_46_out ? 3'b010 : 3'bz;  // Controlled_Buffer controlled_buffer_83
  assign controlled_buffer_23_out = and_37_out ? 3'b001 : 3'bz;  // Controlled_Buffer controlled_buffer_84
  assign controlled_buffer_23_out = and_39_out ? 3'b011 : 3'bz;  // Controlled_Buffer controlled_buffer_85
  assign controlled_buffer_16_out = and_52_out ? F_q_2 : 2'bz;  // Controlled_Buffer controlled_buffer_86
  assign controlled_buffer_16_out = and_47_out ? F_q_4 : 2'bz;  // Controlled_Buffer controlled_buffer_87
  assign controlled_buffer_9_out_2[0] = and_60_out ? 1'b0 : 1'bz;  // Controlled_Buffer controlled_buffer_88
  assign controlled_buffer_9_out_2[0] = and_61_out ? 1'b0 : 1'bz;  // Controlled_Buffer controlled_buffer_89
  assign controlled_buffer_16_out = and_43_out ? controlled_buffer_13_out : 2'bz;  // Controlled_Buffer controlled_buffer_90
  Pull_Resistor pull_resistor_3 (.node(pull_resistor_3_node[0]));
  and and_55 (and_55_out, decoder_1_out0, pull_resistor_3_node[0]);
  assign {controlled_buffer_13_out, controlled_buffer_13_out_2[5], controlled_buffer_13_out_3, controlled_buffer_13_out_2[1:0]} = and_55_out ? W_q : 8'bz;  // Controlled_Buffer controlled_buffer_91
  Multiplexer #(.width(8), .enable("false")) multiplexer_5 (
    .in0({controlled_buffer_13_out, controlled_buffer_13_out_2[5], controlled_buffer_13_out_3, controlled_buffer_13_out_2[1:0]}),
    .in1(demultiplexer_1_out4), .out(multiplexer_5_out), .sel(and_53_out));
  // Probe on W_q
  REG8 W (.C(and_56_out), ._0(RESET_out), .D(multiplexer_5_out), .Q(W_q));
  and and_56 (and_56_out, or_16_out, and_100_out);
  or or_17 (or_17_out, S_q[0], S_q[2]);
  assign controlled_buffer_16_out = and_46_out ? 2'b11 : 2'bz;  // Controlled_Buffer controlled_buffer_92
  assign controlled_buffer_23_out = and_46_out ? 3'b011 : 3'bz;  // Controlled_Buffer controlled_buffer_93
  assign pull_resistor_3_node = and_52_out ? 3'b111 : 3'bz;  // Controlled_Buffer controlled_buffer_94
  assign controlled_buffer_42_out = and_52_out ? 3'b000 : 3'bz;  // Controlled_Buffer controlled_buffer_95
  assign controlled_buffer_42_out[0] = and_47_out ? 1'b0 : 1'bz;  // Controlled_Buffer controlled_buffer_96
  assign pull_resistor_3_node[1] = and_47_out ? 1'b1 : 1'bz;  // Controlled_Buffer controlled_buffer_97
  and and_57 (and_57_out, F_q_3[0], F_q_3[1], F_q_2[0], ~F_q_2[1], and_28_out);  // AND_Gate
  assign controlled_buffer_14_out = and_57_out ? 3'b100 : 3'bz;  // Controlled_Buffer controlled_buffer_98
  assign {pull_resistor_3_node[1:0], pull_resistor_3_node[2]} = and_59_out ? 3'b111 : 3'bz;  // Controlled_Buffer controlled_buffer_99
  and and_58 (and_58_out, F_q_3[0], ~F_q_3[1], F_q_2[0], F_q_2[1], and_28_out);  // AND_Gate
  and and_59 (and_59_out, ~F_q_3[0], F_q_3[1], F_q_4[0], F_q_4[1], and_28_out);  // AND_Gate
  and and_60 (and_60_out, and_16_out, controlled_buffer_13_out[1], controlled_buffer_13_out[0], ~controlled_buffer_13_out_3[1], controlled_buffer_13_out_3[0]);  // AND_Gate
  and and_61 (and_61_out, and_16_out, controlled_buffer_13_out[1], ~controlled_buffer_13_out[0], controlled_buffer_13_out_3[1], controlled_buffer_13_out_3[0]);  // AND_Gate
  and and_62 (and_62_out, ~controlled_buffer_23_out[2], controlled_buffer_23_out[1], controlled_buffer_23_out[0]);  // AND_Gate
  assign controlled_buffer_17_out = and_57_out ? 3'b101 : 3'bz;  // Controlled_Buffer controlled_buffer_100
  assign controlled_buffer_22_out = and_57_out ? 3'b001 : 3'bz;  // Controlled_Buffer controlled_buffer_101
  assign controlled_buffer_16_out = and_59_out ? F_q_2 : 2'bz;  // Controlled_Buffer controlled_buffer_102
  assign {controlled_buffer_42_out[2], controlled_buffer_42_out[0], controlled_buffer_42_out[1]} = and_59_out ? 3'b000 : 3'bz;  // Controlled_Buffer controlled_buffer_103
  assign {controlled_buffer_42_out[2], controlled_buffer_9_out_2[0]} = and_58_out ? 2'b00 : 2'bz;  // Controlled_Buffer controlled_buffer_104
  assign {controlled_buffer_10_out_3[3], pull_resistor_3_node[2:1], controlled_buffer_10_out_3[0]} = and_58_out ? 4'b1111 : 4'bz;  // Controlled_Buffer controlled_buffer_105
  // Probe on controlled_buffer_14_out
  // Probe on controlled_buffer_17_out
  Multiplexer #(.select(3), .width(8)) multiplexer_6 (
    .in0(W_q), .in1(X_q), .in2(Y_q), .in3(Z_q),
    .in4({controlled_buffer_13_out, controlled_buffer_13_out_2[5], controlled_buffer_13_out_3, controlled_buffer_13_out_2[1:0]}),
    .in5({8{1'b0}}), .in6(P_q), .in7(8'h1), .out(multiplexer_6_out), .sel(controlled_buffer_17_out),
    .en(controlled_buffer_10_out_3[3]));
  Decoder #(.select(3), .enable("false")) decoder_2 (
    .out0(decoder_2_out0), .out1(decoder_2_out1), .out2(decoder_2_out2), .out3(decoder_2_out3),
    .out4(decoder_2_out4), .out5(decoder_2_out5), .out6(decoder_2_out6), .out7(decoder_2_out7),
    .sel(controlled_buffer_22_out));
  and and_63 (and_63_out, ~F_q_4[0], ~F_q_4[1], ~F_q_2[0], ~F_q_2[1]);  // AND_Gate
  and and_64 (and_64_out, ~F_q_4[0], F_q_4[1], ~F_q_2[0], ~F_q_2[1], ~S_q[0], ~S_q[2]);  // AND_Gate
  and and_65 (and_65_out, F_q_4[0], F_q_4[1], ~F_q_2[0], ~F_q_2[1], or_17_out);  // AND_Gate
  and and_66 (and_66_out, ~F_q_4[0], ~F_q_4[1], F_q_2[0], ~F_q_2[1], ~S_q[0]);  // AND_Gate
  and and_67 (and_67_out, F_q_4[0], ~F_q_4[1], F_q_2[0], ~F_q_2[1], S_q[0]);  // AND_Gate
  and and_68 (and_68_out, ~F_q_4[0], F_q_4[1], F_q_2[0], ~F_q_2[1], ~S_q[2]);  // AND_Gate
  and and_69 (and_69_out, F_q_4[0], F_q_4[1], F_q_2[0], ~F_q_2[1], S_q[2]);  // AND_Gate
  and and_70 (and_70_out, ~F_q_4[0], ~F_q_4[1], ~F_q_2[0], F_q_2[1], ~S_q[1]);  // AND_Gate
  and and_71 (and_71_out, F_q_4[0], ~F_q_4[1], ~F_q_2[0], F_q_2[1], S_q[1]);  // AND_Gate
  assign {controlled_buffer_42_out[1], controlled_buffer_106_out} = and_72_out ? 3'b000 : 3'bz;  // Controlled_Buffer controlled_buffer_106
  and and_72 (and_72_out, and_26_out, ~F_q_2[1], F_q_2[0], F_q_3[1], F_q_3[0]);  // AND_Gate
  and and_73 (and_73_out, F_q_3[0], ~F_q_3[1], F_q_2[0], ~F_q_2[1], and_28_out);  // AND_Gate
  and and_74 (and_74_out, ~F_q_3[0], F_q_3[1], F_q_4[0], ~F_q_4[1], and_28_out);  // AND_Gate
  assign controlled_buffer_10_out_3[3] = and_57_out ? and_57_out : 1'bz;  // Controlled_Buffer controlled_buffer_107
  assign controlled_buffer_22_out = and_58_out ? 3'b000 : 3'bz;  // Controlled_Buffer controlled_buffer_108
  assign controlled_buffer_14_out = and_58_out ? 3'b011 : 3'bz;  // Controlled_Buffer controlled_buffer_109
  and and_75 (and_75_out, and_16_out, controlled_buffer_13_out_2[5], controlled_buffer_13_out_3[2], controlled_buffer_13_out_3[1], ~controlled_buffer_13_out_3[0]);  // AND_Gate
  and and_76 (and_76_out, and_16_out, ~controlled_buffer_13_out[1], controlled_buffer_13_out[0], controlled_buffer_13_out_3[1], controlled_buffer_13_out_3[0]);  // AND_Gate
  assign controlled_buffer_9_out_2[0] = or_19_out ? 1'b0 : 1'bz;  // Controlled_Buffer controlled_buffer_110
  // Probe on controlled_buffer_23_out
  assign {controlled_buffer_13_out, controlled_buffer_13_out_2[5], controlled_buffer_13_out_3, controlled_buffer_13_out_2[1:0]} = not_2_out ? controlled_buffer_112_out : 8'bz;  // Controlled_Buffer controlled_buffer_111
  assign controlled_buffer_112_out = and_78_out ? demultiplexer_1_out1 : 8'bz;  // Controlled_Buffer controlled_buffer_112
  Multiplexer #(.select(3), .width(8)) multiplexer_7 (
    .in0(W_q), .in1(X_q), .in2(Y_q), .in3(Z_q),
    .in4({controlled_buffer_13_out, controlled_buffer_13_out_2[5], controlled_buffer_13_out_3, controlled_buffer_13_out_2[1:0]}),
    .in5({8{1'b0}}), .in6(P_q), .out(multiplexer_7_out), .sel(controlled_buffer_14_out),
    .en(controlled_buffer_10_out_3[3]));  // open: in7
  Demultiplexer #(.select(3), .width(8)) demultiplexer_1 (
    .out0(demultiplexer_1_out0), .out1(demultiplexer_1_out1), .out2(demultiplexer_1_out2),
    .out3(demultiplexer_1_out3), .out4(demultiplexer_1_out4), .out5(demultiplexer_1_out5),
    .out6(demultiplexer_1_out6), .out7(demultiplexer_1_out7), .in(alu_1_r), .sel(controlled_buffer_23_out),
    .en(controlled_buffer_10_out_3[3]));
  // Probe on alu_1_r
  or or_18 (or_18_out, and_71_out, and_70_out, and_69_out, and_68_out, and_67_out, and_66_out, and_65_out, and_64_out, and_63_out, and_81_out, and_82_out, and_83_out, and_84_out, and_85_out, and_86_out);
  assign {controlled_buffer_113_out[2], pull_resistor_3_node[2], controlled_buffer_113_out[0]} = and_72_out ? 3'b111 : 3'bz;  // Controlled_Buffer controlled_buffer_113
  assign {controlled_buffer_42_out[2], controlled_buffer_9_out_2[0], controlled_buffer_42_out[0]} = and_57_out ? 3'b000 : 3'bz;  // Controlled_Buffer controlled_buffer_114
  assign controlled_buffer_23_out = and_58_out ? 3'b111 : 3'bz;  // Controlled_Buffer controlled_buffer_115
  or or_19 (or_19_out, and_76_out, and_75_out);
  assign {controlled_buffer_10_out_3[0], controlled_buffer_10_out_3[3]} = or_19_out ? 2'b11 : 2'bz;  // Controlled_Buffer controlled_buffer_116
  assign controlled_buffer_14_out = or_19_out ? 3'b011 : 3'bz;  // Controlled_Buffer controlled_buffer_117
  Pull_Resistor pull_resistor_4 (.node(controlled_buffer_23_out));
  Pull_Resistor #(.pull(1)) pull_resistor_5 (.node(controlled_buffer_9_out_2[0]));
  Pull_Resistor pull_resistor_6 (.node(controlled_buffer_113_out[2]));
  Pull_Resistor pull_resistor_7 (.node(controlled_buffer_10_out_3[3]));
  and and_77 (and_77_out, ~controlled_buffer_23_out[0], controlled_buffer_23_out[1], ~controlled_buffer_23_out[2]);  // AND_Gate
  not not_2 (not_2_out, controlled_buffer_42_out[1]);
  and and_78 (and_78_out, controlled_buffer_23_out[0], ~controlled_buffer_23_out[1], ~controlled_buffer_23_out[2]);  // AND_Gate
  and and_79 (and_79_out, controlled_buffer_10_out_3[3], ~controlled_buffer_23_out[0], ~controlled_buffer_23_out[1], ~controlled_buffer_23_out[2]);  // AND_Gate
  ALU alu_1 (
    .LSR(decoder_2_out6), .LSL(decoder_2_out7), .NOT(decoder_2_out3), .OR(decoder_2_out4),
    .AND(decoder_2_out5), .ADD(decoder_2_out1), .SUB(decoder_2_out2), .A(multiplexer_7_out),
    .B(multiplexer_6_out), .R(alu_1_r), .C(alu_1_c[0]), .INC(decoder_2_out0), .V(alu_1_c[1]), .Z(alu_1_c[2]),
    .N(alu_1_c[3]));
  assign {controlled_buffer_10_out_3[3], controlled_buffer_10_out_2[0]} = and_80_out ? 2'b11 : 2'bz;  // Controlled_Buffer controlled_buffer_118
  and and_80 (and_80_out, and_54_out, or_18_out);
  or or_20 (or_20_out, and_73_out, and_74_out);
  assign controlled_buffer_16_out = and_58_out ? F_q_4 : 2'bz;  // Controlled_Buffer controlled_buffer_119
  assign controlled_buffer_17_out = or_19_out ? 3'b111 : 3'bz;  // Controlled_Buffer controlled_buffer_120
  assign controlled_buffer_121_out = controlled_buffer_10_out_3[3] ? {4'b0000, alu_1_c} : 8'bz;  // Controlled_Buffer controlled_buffer_121
  assign {controlled_buffer_9_out_2[0], controlled_buffer_42_out[2]} = and_80_out ? 2'b00 : 2'bz;  // Controlled_Buffer controlled_buffer_122
  and and_81 (and_81_out, ~F_q_4[0], F_q_4[0], ~F_q_4[0], F_q_4[1], ~S_q[3]);  // AND_Gate
  and and_82 (and_82_out, F_q_4[0], F_q_4[0], ~F_q_4[0], F_q_4[1], S_q[3]);  // AND_Gate
  and and_83 (and_83_out, ~F_q_4[0], ~F_q_4[0], F_q_4[0], F_q_4[1], or_21_out);  // AND_Gate
  and and_84 (and_84_out, F_q_4[0], ~F_q_4[0], F_q_4[1], F_q_2[0], or_22_out);  // AND_Gate
  and and_85 (and_85_out, ~F_q_4[0], F_q_4[1], F_q_2[0], F_q_2[1], or_23_out);  // AND_Gate
  and and_86 (and_86_out, F_q_4[0], F_q_4[1], F_q_2[0], F_q_2[1], or_24_out);
  assign {controlled_buffer_123_out[1], controlled_buffer_42_out[0]} = or_20_out ? 2'b00 : 2'bz;  // Controlled_Buffer controlled_buffer_123
  assign {controlled_buffer_124_out[1], controlled_buffer_10_out_3[0]} = or_20_out ? 2'b11 : 2'bz;  // Controlled_Buffer controlled_buffer_124
  assign controlled_buffer_23_out = or_19_out ? 3'b011 : 3'bz;  // Controlled_Buffer controlled_buffer_125
  assign controlled_buffer_22_out = or_19_out ? 3'b010 : 3'bz;  // Controlled_Buffer controlled_buffer_126
  assign controlled_buffer_17_out = and_80_out ? 3'b100 : 3'bz;  // Controlled_Buffer controlled_buffer_127
  assign controlled_buffer_22_out = and_80_out ? 3'b001 : 3'bz;  // Controlled_Buffer controlled_buffer_128
  or or_21 (or_21_out, and_87_out, and_88_out);
  or or_22 (or_22_out, and_89_out, and_90_out);
  or or_23 (or_23_out, and_91_out, and_92_out);
  or or_24 (or_24_out, and_93_out, S_q[2], and_94_out);
  assign controlled_buffer_23_out = and_80_out ? 3'b010 : 3'bz;  // Controlled_Buffer controlled_buffer_129
  assign controlled_buffer_14_out = and_80_out ? 3'b110 : 3'bz;  // Controlled_Buffer controlled_buffer_130
  and and_87 (and_87_out, ~S_q[1], ~S_q[3]);  // AND_Gate
  and and_88 (and_88_out, S_q[1], S_q[3]);
  and and_89 (and_89_out, S_q[1], ~S_q[3]);  // AND_Gate
  and and_90 (and_90_out, ~S_q[1], S_q[3]);  // AND_Gate
  and and_91 (and_91_out, S_q[1], ~S_q[2], S_q[3]);  // AND_Gate
  and and_92 (and_92_out, ~S_q[1], ~S_q[2], ~S_q[3]);  // AND_Gate
  and and_93 (and_93_out, ~S_q[1], S_q[3]);  // AND_Gate
  and and_94 (and_94_out, S_q[1], ~S_q[3]);  // AND_Gate
  assign {controlled_buffer_13_out, controlled_buffer_13_out_2[5], controlled_buffer_13_out_3, controlled_buffer_13_out_2[1:0]} = controlled_buffer_113_out[2] ? R_2_q : 8'bz;  // Controlled_Buffer controlled_buffer_131
  and and_95 (and_95_out, controlled_buffer_10_out_3[3], controlled_buffer_9_out_2[0]);
  // Probe on R_2_q
  REG8 R_2 (.C(and_96_out), ._0(RESET_out), .D(demultiplexer_1_out0), .Q(R_2_q));
  and and_96 (and_96_out, and_79_out, and_100_out);
  // Probe on S_q
  REG8 S (.C(and_97_out), ._0(RESET_out), .D(controlled_buffer_121_out), .Q(S_q));
  and and_97 (and_97_out, and_95_out, and_100_out);
  or or_25 (or_25_out, ~and_100_out, pull_resistor_3_node[2]);  // OR_Gate
  Pull_Resistor pull_resistor_8 (.node(controlled_buffer_10_out_3[0]));
  Pull_Resistor #(.pull(1)) pull_resistor_9 (.node(controlled_buffer_42_out[0]));
  Pull_Resistor pull_resistor_10 (.node(pull_resistor_3_node[2]));
  Multiplexer #(.width(8), .enable("false")) multiplexer_8 (
    .in0({controlled_buffer_13_out, controlled_buffer_13_out_2[5], controlled_buffer_13_out_3, controlled_buffer_13_out_2[1:0]}),
    .in1(demultiplexer_1_out2), .out(multiplexer_8_out), .sel(and_77_out));
  Multiplexer #(.width(8), .enable("false")) multiplexer_9 (
    .in0({controlled_buffer_13_out, controlled_buffer_13_out_2[5], controlled_buffer_13_out_3, controlled_buffer_13_out_2[1:0]}),
    .in1(demultiplexer_1_out3), .out(multiplexer_9_out), .sel(and_62_out));
  // Probe on A_2_q
  REG8 A_2 (.C(and_98_out), ._0(RESET_out), .D(multiplexer_9_out), .Q(A_2_q));
  and and_98 (and_98_out, controlled_buffer_10_out_3[0], ~or_25_out);  // AND_Gate
  Pull_Resistor #(.pull(1)) pull_resistor_11 (.node(controlled_buffer_42_out[2]));
  Pull_Resistor #(.pull(1)) pull_resistor_12 (.node(controlled_buffer_15_out[0]));
  Pull_Resistor #(.pull(1)) pull_resistor_13 (.node(controlled_buffer_42_out[1]));
  Pull_Resistor pull_resistor_14 (.node(controlled_buffer_10_out_2[0]));
  COUTER8 P (
    .I(controlled_buffer_42_out[2]), .D(multiplexer_8_out), .W(controlled_buffer_10_out_2[0]),
    .C(and_100_out), .R(RESET_out), .Q(P_q));
  REG8 F (
    .C(and_99_out), ._0(RESET_out),
    .D({controlled_buffer_13_out, controlled_buffer_13_out_2[5], controlled_buffer_13_out_3, controlled_buffer_13_out_2[1:0]}),
    .Q({F_q_2, F_q_4, F_q_3, F_q}));
  and and_99 (and_99_out, controlled_buffer_42_out[0], and_100_out);
  // Probe on {controlled_buffer_13_out, controlled_buffer_13_out_2[5], controlled_buffer_13_out_3, controlled_buffer_13_out_2[1:0]}
  // Probe on P_q
  assign {controlled_buffer_13_out, controlled_buffer_13_out_2[5], controlled_buffer_13_out_3, controlled_buffer_13_out_2[1:0]} = controlled_buffer_42_out[1] ? multiplexer_10_out : 8'bz;  // Controlled_Buffer controlled_buffer_132
  // Probe on {F_q_2, F_q_4, F_q_3, F_q}
  // Probe on multiplexer_11_out
  Multiplexer #(.width(8), .enable("false")) multiplexer_10 (
    .in0(ram16_1_out), .in1(8'haf), .out(multiplexer_10_out), .sel(or_27_out));
  Pull_Resistor pull_resistor_15 (.node(controlled_buffer_11_out));
  Multiplexer #(.width(8), .enable("false")) multiplexer_11 (
    .in0(P_q), .in1(A_2_q), .out(multiplexer_11_out), .sel(pull_resistor_3_node[2]));
  not not_3 (not_3_out, controlled_buffer_42_out[1]);
  assign controlled_buffer_133_out = not_3_out ? {controlled_buffer_13_out, controlled_buffer_13_out_2[5], controlled_buffer_13_out_3, controlled_buffer_13_out_2[1:0]} : 8'bz;  // Controlled_Buffer controlled_buffer_133
  and and_100 (and_100_out, CLOCK_out, ~controlled_buffer_11_out);  // AND_Gate
  or or_26 (or_26_out, dec4_1__0_2, dec4_1__1_2, dec4_1__2_2, dec4_1__3_2);
  DEC4 dec4_1 (
    ._0(multiplexer_11_out[4]), ._1(multiplexer_11_out[5]), ._2(multiplexer_11_out[6]),
    ._3(multiplexer_11_out[7]), ._0_2(dec4_1__0_2), ._1_2(dec4_1__1_2), ._2_2(dec4_1__2_2),
    ._3_2(dec4_1__3_2), ._4(dec4_1__4), ._5(dec4_1__5), ._6(dec4_1__6), ._7(dec4_1__7), ._8(dec4_1__8),
    ._9(dec4_1__9), .A(dec4_1_a), .B(dec4_1_b), .C(dec4_1_c), .D(dec4_1_d), .E_2(dec4_1_e_2), .F(dec4_1_f),
    .E(controlled_buffer_15_out[0]));
  Button RESET (.out(RESET_out));
  Clock CLOCK (.out(CLOCK_out));
  LED HALT (.in(controlled_buffer_11_out));
  RAM16 ram16_1 (
    .SELECT(dec4_1_f), .CLOCK(and_100_out), .READ(controlled_buffer_42_out[1]), .RESET(RESET_out),
    .ADDRESS(multiplexer_11_out[3:0]), .IN(controlled_buffer_133_out), .OUT(ram16_1_out));
  ROM #(.addrWidth(6)) rom_1 (.addr(multiplexer_11_out[5:0]), .data(ram16_1_out), .sel(or_26_out));
  or or_27 (or_27_out, dec4_1__4, dec4_1__5, dec4_1__6, dec4_1__7, dec4_1__8, dec4_1__9, dec4_1_a, dec4_1_b, dec4_1_c, dec4_1_d, dec4_1_e_2);

  // Notes on the sheet:
  //   JSR
  //   JSR
  //   RM
  //   RR
  //   JMP
  //   Bcc
  //   JSR
  //   RR
  //   DST
  //   DIR
  //   JSR
  //   DST
  //   DST
  //   RI
  //   SRC
  //   DST
  //   OP
  //   JMP
  //   SRC
  //   RM
  //   DST
  //   DST
  //   DST
  //   DST
  //   SRC
  //   Bcc
  //   ANY
  //   !C and !Z
  //   C or Z
  //   !C
  //   C
  //   !Z
  //   Z
  //   !V
  //   V
  //   DST
  //   SRC
  //   PUSH REG
  //   POP REG
  //   OP
  //   DST
  //   DST
  //   PUSH IMM
  //   POP REG
  //   POP
  //   BRA
  //   HI
  //   LS
  //   CC
  //   CS
  //   NE
  //   EQ
  //   VC
  //   VS
  //   RM
  //   MR
  //   SRC
  //   PUSH REG
  //   PUSH IMM
  //   PL
  //   MI
  //   GE
  //   LT
  //   GT
  //   LE
  //   ARITHMETIC
  //   (N and V) or (!N and !V)
  //   (N and !V) or (!N and V)
  //   (N and V and !Z) or (!N and !V and !Z)
  //   Z or (N and !V) or (!N and V)
  //   MOVES
  //   DST
  //   CONTROL
  //   !N
  //   N
  //   contents of rom_1 (hex, n*v repeats v):
  //   3d ff d 2 e 8 bd cf c7 0 62 4 d 1 1e 28 1 39 e 8 21 d5 d7 0 62 3 81 1e 84 68 1 2 f6
  //   NON-EXISTING
  //   ADDRESSES
endmodule

module ALU (
  input  LSR,
  input  LSL,
  input  NOT,
  input  OR,
  input  AND,
  input  ADD,
  input  SUB,
  input  INC,
  input  [7:0] A,
  input  [7:0] B,
  output N,
  output Z,
  output V,
  output C,
  output [7:0] R
);

  wire add8_1_c_2, and_2_out, and_3_out, lsl_1_c, lsr_1_c, multiplexer_2_out, not_2_out, not_3_out, or_2_out,
       or_3_out, or_4_out;
  wire [1:0] controlled_buffer_7_out;
  wire [7:0] add8_1_r, and_1_out, bit_extender_1_out, lsl_1_o, lsr_1_o, multiplexer_1_out, not_1_out,
       or_1_out, xor_1_out;

  Multiplexer #(.width(8), .enable("false")) multiplexer_1 (.in0(B), .in1(8'h1), .out(multiplexer_1_out), .sel(INC));
  // Probe on multiplexer_1_out
  LSR lsr_1 (.I(A), .O(lsr_1_o), .C(lsr_1_c));
  LSL lsl_1 (.O(lsl_1_o), .I(A), .C(lsl_1_c));
  assign {N, R[6:0]} = LSR ? lsr_1_o : 8'bz;  // Controlled_Buffer controlled_buffer_1
  assign {N, R[6:0]} = LSL ? lsl_1_o : 8'bz;  // Controlled_Buffer controlled_buffer_2
  assign not_1_out = ~A;  // NOT_Gate not_1, 8 bits wide
  assign {N, R[6:0]} = NOT ? not_1_out : 8'bz;  // Controlled_Buffer controlled_buffer_3
  assign or_1_out = A | multiplexer_1_out;  // OR_Gate or_1, 8 bits wide
  assign {N, R[6:0]} = OR ? or_1_out : 8'bz;  // Controlled_Buffer controlled_buffer_4
  assign and_1_out = A & multiplexer_1_out;  // AND_Gate and_1, 8 bits wide
  assign {N, R[6:0]} = AND ? and_1_out : 8'bz;  // Controlled_Buffer controlled_buffer_5
  assign bit_extender_1_out = {{7{SUB}}, SUB};  // Bit_Extender bit_extender_1
  assign xor_1_out = multiplexer_1_out ^ bit_extender_1_out;  // XOR_Gate xor_1, 8 bits wide
  or or_2 (or_2_out, INC, SUB, ADD);
  ADD8 add8_1 (.C(SUB), .A(A), .B(xor_1_out), .R(add8_1_r), .C_2(add8_1_c_2));
  assign {N, R[6:0]} = or_2_out ? add8_1_r : 8'bz;  // Controlled_Buffer controlled_buffer_6
  not not_2 (not_2_out, add8_1_c_2);
  assign controlled_buffer_7_out = LSR ? 2'b10 : 2'bz;  // Controlled_Buffer controlled_buffer_7
  assign controlled_buffer_7_out = LSL ? 2'b01 : 2'bz;  // Controlled_Buffer controlled_buffer_8
  assign controlled_buffer_7_out = NOT ? 2'b11 : 2'bz;  // Controlled_Buffer controlled_buffer_9
  assign controlled_buffer_7_out = OR ? 2'b11 : 2'bz;  // Controlled_Buffer controlled_buffer_10
  assign controlled_buffer_7_out = AND ? 2'b11 : 2'bz;  // Controlled_Buffer controlled_buffer_11
  Multiplexer #(.enable("false")) multiplexer_2 (.in0(add8_1_c_2), .in1(not_2_out), .out(multiplexer_2_out), .sel(SUB));
  or or_3 (or_3_out, R[4], N, R[6], R[5], R[3], R[2], R[1], R[0]);
  and and_2 (and_2_out, ~N, A[7], xor_1_out[7]);  // AND_Gate
  and and_3 (and_3_out, N, ~A[7], ~xor_1_out[7]);  // AND_Gate
  not not_3 (not_3_out, or_2_out);
  not not_4 (Z, or_3_out);
  Multiplexer #(.select(2), .enable("false")) multiplexer_3 (
    .in0(multiplexer_2_out), .in1(lsl_1_c), .in2(lsr_1_c), .in3(1'b0), .out(C), .sel(controlled_buffer_7_out));
  or or_4 (or_4_out, and_3_out, and_2_out);
  Multiplexer #(.enable("false")) multiplexer_4 (.in0(or_4_out), .in1(1'b0), .out(V), .sel(not_3_out));
  Pull_Resistor pull_resistor_1 (.node(controlled_buffer_7_out));

  assign R[7] = N;
endmodule

module ADD1 (
  input  Ci,
  input  A,
  input  B,
  output R,
  output Co
);

  wire and_1_out, and_2_out, xor_1_out;

  and and_1 (and_1_out, A, B);
  xor xor_1 (xor_1_out, A, B);
  xor xor_2 (R, Ci, xor_1_out);
  and and_2 (and_2_out, Ci, xor_1_out);
  or or_1 (Co, and_2_out, and_1_out);
endmodule

module ADD8 (
  input  C,
  input  [7:0] A,
  input  [7:0] B,
  output [7:0] R,
  output C_2
);

  wire add1_1_co, add1_2_co, add1_3_co, add1_4_co, add1_5_co, add1_6_co, add1_7_co;

  ADD1 add1_1 (.A(A[0]), .B(B[0]), .R(R[0]), .Ci(C), .Co(add1_1_co));
  ADD1 add1_2 (.A(A[1]), .B(B[1]), .R(R[1]), .Ci(add1_1_co), .Co(add1_2_co));
  ADD1 add1_3 (.A(A[2]), .B(B[2]), .R(R[2]), .Ci(add1_2_co), .Co(add1_3_co));
  ADD1 add1_4 (.A(A[3]), .B(B[3]), .R(R[3]), .Ci(add1_3_co), .Co(add1_4_co));
  ADD1 add1_5 (.A(A[4]), .B(B[4]), .R(R[4]), .Ci(add1_4_co), .Co(add1_5_co));
  ADD1 add1_6 (.A(A[5]), .B(B[5]), .R(R[5]), .Ci(add1_5_co), .Co(add1_6_co));
  ADD1 add1_7 (.A(A[6]), .B(B[6]), .R(R[6]), .Ci(add1_6_co), .Co(add1_7_co));
  ADD1 add1_8 (.A(A[7]), .B(B[7]), .R(R[7]), .Ci(add1_7_co), .Co(C_2));
endmodule

module LSL (
  input  [7:0] I,
  output [7:0] O,
  output C
);


  assign C = I[7];
  assign O = {I[6:0], 1'b0};
endmodule

module LSR (
  input  [7:0] I,
  output C,
  output [7:0] O
);


  assign C = I[0];
  assign O = {1'b0, I[7:1]};
endmodule

module SR_LATCH (
  input  S,
  input  E,
  input  R,
  output Q
);

  wire and_1_out, and_2_out, nor_1_out;

  and and_1 (and_1_out, S, E);
  and and_2 (and_2_out, E, R);
  nor nor_1 (nor_1_out, and_1_out, Q);
  nor nor_2 (Q, nor_1_out, and_2_out);
endmodule

module D_LATCH (
  input  D,
  input  E,
  input  _0,
  output Q
);

  wire and_1_out, and_2_out, nor_1_out, or_1_out;

  and and_1 (and_1_out, D, E);
  and and_2 (and_2_out, E, ~D);  // AND_Gate
  or or_1 (or_1_out, and_2_out, _0);
  nor nor_1 (nor_1_out, and_1_out, Q);
  nor nor_2 (Q, nor_1_out, or_1_out);
endmodule

module D_FLIP_FLOP (
  input  D,
  input  C,
  input  R,
  output Q
);

  wire and_1_out, and_2_out, and_3_out, and_4_out, nor_1_out, nor_2_out, nor_3_out, not_1_out, or_1_out,
       or_2_out;

  and and_1 (and_1_out, D, C);
  and and_2 (and_2_out, C, ~D);  // AND_Gate
  nor nor_1 (nor_1_out, and_1_out, nor_2_out);
  nor nor_2 (nor_2_out, nor_1_out, or_1_out);
  or or_1 (or_1_out, and_2_out, R);
  not not_1 (not_1_out, C);
  and and_3 (and_3_out, nor_2_out, not_1_out);
  and and_4 (and_4_out, not_1_out, ~nor_2_out);  // AND_Gate
  nor nor_3 (nor_3_out, and_3_out, Q);
  nor nor_4 (Q, nor_3_out, or_2_out);
  or or_2 (or_2_out, and_4_out, R);
endmodule

module REG8 (
  input  C,
  input  _0,
  input  [7:0] D,
  output [7:0] Q
);

  D_FLIP_FLOP d_flip_flop_1 (.D(D[6]), .C(C), .R(_0), .Q(Q[6]));
  D_FLIP_FLOP d_flip_flop_2 (.D(D[7]), .C(C), .R(_0), .Q(Q[7]));
  D_FLIP_FLOP d_flip_flop_3 (.D(D[5]), .C(C), .R(_0), .Q(Q[5]));
  D_FLIP_FLOP d_flip_flop_4 (.D(D[4]), .C(C), .R(_0), .Q(Q[4]));
  D_FLIP_FLOP d_flip_flop_5 (.D(D[2]), .C(C), .R(_0), .Q(Q[2]));
  D_FLIP_FLOP d_flip_flop_6 (.D(D[3]), .C(C), .R(_0), .Q(Q[3]));
  D_FLIP_FLOP d_flip_flop_7 (.D(D[1]), .C(C), .R(_0), .Q(Q[1]));
  D_FLIP_FLOP d_flip_flop_8 (.D(D[0]), .C(C), .R(_0), .Q(Q[0]));

  // Notes on the sheet:
  //   7
  //   0
endmodule

module RAM16 (
  input  SELECT,
  input  CLOCK,
  input  READ,
  input  RESET,
  input  [3:0] ADDRESS,
  input  [7:0] IN,
  output [7:0] OUT
);

  wire and_1_out, and_2_out, and_3_out, and_4_out, and_5_out, and_6_out, and_7_out, and_8_out, and_9_out,
       and_10_out, and_11_out, and_12_out, and_13_out, and_14_out, and_15_out, and_16_out, and_17_out,
       and_18_out, and_19_out, and_20_out, and_21_out, and_22_out, and_23_out, and_24_out, and_25_out,
       and_26_out, and_27_out, and_28_out, and_29_out, and_30_out, and_31_out, and_32_out, dec4_1__0_2,
       dec4_1__1_2, dec4_1__2_2, dec4_1__3_2, dec4_1__4, dec4_1__5, dec4_1__6, dec4_1__7, dec4_1__8,
       dec4_1__9, dec4_1_a, dec4_1_b, dec4_1_c, dec4_1_d, dec4_1_e_2, dec4_1_f;
  wire [7:0] reg8_1_q, reg8_2_q, reg8_3_q, reg8_4_q, reg8_5_q, reg8_6_q, reg8_7_q, reg8_8_q, reg8_9_q,
       reg8_10_q, reg8_11_q, reg8_12_q, reg8_13_q, reg8_14_q, reg8_15_q, reg8_16_q;

  REG8 reg8_1 (.C(and_1_out), ._0(RESET), .D(IN), .Q(reg8_1_q));
  and and_1 (and_1_out, dec4_1_f, CLOCK);
  REG8 reg8_2 (.C(and_2_out), ._0(RESET), .D(IN), .Q(reg8_2_q));
  and and_2 (and_2_out, dec4_1_e_2, CLOCK);
  REG8 reg8_3 (.C(and_3_out), ._0(RESET), .D(IN), .Q(reg8_3_q));
  and and_3 (and_3_out, dec4_1_d, CLOCK);
  REG8 reg8_4 (.C(and_4_out), ._0(RESET), .D(IN), .Q(reg8_4_q));
  and and_4 (and_4_out, dec4_1_c, CLOCK);
  REG8 reg8_5 (.C(and_5_out), ._0(RESET), .D(IN), .Q(reg8_5_q));
  and and_5 (and_5_out, dec4_1_b, CLOCK);
  REG8 reg8_6 (.C(and_6_out), ._0(RESET), .D(IN), .Q(reg8_6_q));
  and and_6 (and_6_out, dec4_1_a, CLOCK);
  REG8 reg8_7 (.C(and_7_out), ._0(RESET), .D(IN), .Q(reg8_7_q));
  and and_7 (and_7_out, dec4_1__9, CLOCK);
  REG8 reg8_8 (.C(and_8_out), ._0(RESET), .D(IN), .Q(reg8_8_q));
  and and_8 (and_8_out, dec4_1__8, CLOCK);
  DEC4 dec4_1 (
    ._0(ADDRESS[0]), ._1(ADDRESS[1]), ._2(ADDRESS[2]), ._3(ADDRESS[3]), ._0_2(dec4_1__0_2),
    ._1_2(dec4_1__1_2), ._2_2(dec4_1__2_2), ._3_2(dec4_1__3_2), ._4(dec4_1__4), ._5(dec4_1__5),
    ._6(dec4_1__6), ._7(dec4_1__7), ._8(dec4_1__8), ._9(dec4_1__9), .A(dec4_1_a), .B(dec4_1_b), .C(dec4_1_c),
    .D(dec4_1_d), .E_2(dec4_1_e_2), .F(dec4_1_f), .E(SELECT));
  assign OUT = and_9_out ? reg8_1_q : 8'bz;  // Controlled_Buffer controlled_buffer_1
  // Probe on reg8_1_q
  and and_9 (and_9_out, dec4_1_f, READ);
  assign OUT = and_10_out ? reg8_2_q : 8'bz;  // Controlled_Buffer controlled_buffer_2
  // Probe on reg8_2_q
  and and_10 (and_10_out, dec4_1_e_2, READ);
  assign OUT = and_11_out ? reg8_3_q : 8'bz;  // Controlled_Buffer controlled_buffer_3
  // Probe on reg8_3_q
  and and_11 (and_11_out, dec4_1_d, READ);
  assign OUT = and_12_out ? reg8_4_q : 8'bz;  // Controlled_Buffer controlled_buffer_4
  // Probe on reg8_4_q
  and and_12 (and_12_out, dec4_1_c, READ);
  assign OUT = and_13_out ? reg8_5_q : 8'bz;  // Controlled_Buffer controlled_buffer_5
  // Probe on reg8_5_q
  and and_13 (and_13_out, dec4_1_b, READ);
  assign OUT = and_14_out ? reg8_6_q : 8'bz;  // Controlled_Buffer controlled_buffer_6
  // Probe on reg8_6_q
  and and_14 (and_14_out, dec4_1_a, READ);
  assign OUT = and_15_out ? reg8_7_q : 8'bz;  // Controlled_Buffer controlled_buffer_7
  // Probe on reg8_7_q
  and and_15 (and_15_out, dec4_1__9, READ);
  assign OUT = and_16_out ? reg8_8_q : 8'bz;  // Controlled_Buffer controlled_buffer_8
  // Probe on reg8_8_q
  and and_16 (and_16_out, dec4_1__8, READ);
  and and_17 (and_17_out, dec4_1__0_2, READ);
  assign OUT = and_17_out ? reg8_9_q : 8'bz;  // Controlled_Buffer controlled_buffer_9
  and and_18 (and_18_out, dec4_1__1_2, READ);
  assign OUT = and_18_out ? reg8_10_q : 8'bz;  // Controlled_Buffer controlled_buffer_10
  and and_19 (and_19_out, dec4_1__2_2, READ);
  assign OUT = and_19_out ? reg8_11_q : 8'bz;  // Controlled_Buffer controlled_buffer_11
  and and_20 (and_20_out, dec4_1__3_2, READ);
  assign OUT = and_20_out ? reg8_12_q : 8'bz;  // Controlled_Buffer controlled_buffer_12
  and and_21 (and_21_out, dec4_1__4, READ);
  assign OUT = and_21_out ? reg8_13_q : 8'bz;  // Controlled_Buffer controlled_buffer_13
  and and_22 (and_22_out, dec4_1__5, READ);
  assign OUT = and_22_out ? reg8_14_q : 8'bz;  // Controlled_Buffer controlled_buffer_14
  and and_23 (and_23_out, dec4_1__6, READ);
  assign OUT = and_23_out ? reg8_15_q : 8'bz;  // Controlled_Buffer controlled_buffer_15
  and and_24 (and_24_out, dec4_1__7, READ);
  assign OUT = and_24_out ? reg8_16_q : 8'bz;  // Controlled_Buffer controlled_buffer_16
  // Probe on reg8_9_q
  REG8 reg8_9 (.C(and_25_out), ._0(RESET), .D(IN), .Q(reg8_9_q));
  // Probe on reg8_10_q
  REG8 reg8_10 (.C(and_26_out), ._0(RESET), .D(IN), .Q(reg8_10_q));
  // Probe on reg8_11_q
  REG8 reg8_11 (.C(and_27_out), ._0(RESET), .D(IN), .Q(reg8_11_q));
  // Probe on reg8_12_q
  REG8 reg8_12 (.C(and_28_out), ._0(RESET), .D(IN), .Q(reg8_12_q));
  // Probe on reg8_13_q
  REG8 reg8_13 (.C(and_29_out), ._0(RESET), .D(IN), .Q(reg8_13_q));
  // Probe on reg8_14_q
  REG8 reg8_14 (.C(and_30_out), ._0(RESET), .D(IN), .Q(reg8_14_q));
  // Probe on reg8_15_q
  REG8 reg8_15 (.C(and_31_out), ._0(RESET), .D(IN), .Q(reg8_15_q));
  // Probe on reg8_16_q
  REG8 reg8_16 (.C(and_32_out), ._0(RESET), .D(IN), .Q(reg8_16_q));
  and and_25 (and_25_out, dec4_1__0_2, CLOCK);
  and and_26 (and_26_out, dec4_1__1_2, CLOCK);
  and and_27 (and_27_out, dec4_1__2_2, CLOCK);
  and and_28 (and_28_out, dec4_1__3_2, CLOCK);
  and and_29 (and_29_out, dec4_1__4, CLOCK);
  and and_30 (and_30_out, dec4_1__5, CLOCK);
  and and_31 (and_31_out, dec4_1__6, CLOCK);
  and and_32 (and_32_out, dec4_1__7, CLOCK);

  // Notes on the sheet:
  //   OUT
  //   IN
endmodule

module DEC2 (
  input  _0,
  input  _1,
  input  E,
  output out_4,
  output out_5,
  output out_6,
  output out_7
);

  and and_1 (out_4, ~_0, ~_1, E);  // AND_Gate
  and and_2 (out_5, _0, ~_1, E);  // AND_Gate
  and and_3 (out_6, ~_0, _1, E);  // AND_Gate
  and and_4 (out_7, _0, _1, E);
endmodule

module DEC4 (
  input  _0,
  input  _1,
  input  _2,
  input  _3,
  input  E,
  output _0_2,
  output _1_2,
  output _2_2,
  output _3_2,
  output _4,
  output _5,
  output _6,
  output _7,
  output _8,
  output _9,
  output A,
  output B,
  output C,
  output D,
  output E_2,
  output F
);

  wire dec2_1_out_4, dec2_1_out_5, dec2_1_out_6, dec2_1_out_7;

  DEC2 dec2_1 (
    ._0(_2), ._1(_3), .out_4(dec2_1_out_4), .out_5(dec2_1_out_5), .out_6(dec2_1_out_6), .out_7(dec2_1_out_7),
    .E(E));
  DEC2 dec2_2 (._0(_0), ._1(_1), .out_4(_0_2), .out_5(_1_2), .out_6(_2_2), .out_7(_3_2), .E(dec2_1_out_4));
  DEC2 dec2_3 (._0(_0), ._1(_1), .out_4(_4), .out_5(_5), .out_6(_6), .out_7(_7), .E(dec2_1_out_5));
  DEC2 dec2_4 (._0(_0), ._1(_1), .out_4(_8), .out_5(_9), .out_6(A), .out_7(B), .E(dec2_1_out_6));
  DEC2 dec2_5 (._0(_0), ._1(_1), .out_4(C), .out_5(D), .out_6(E_2), .out_7(F), .E(dec2_1_out_7));
endmodule

module TOGGLE (
  input  C,
  input  R,
  input  T,
  input  W,
  input  D,
  output Q
);

  wire multiplexer_1_out, multiplexer_2_out, not_1_out;

  D_FLIP_FLOP d_flip_flop_1 (.D(multiplexer_1_out), .C(C), .R(R), .Q(Q));
  Multiplexer #(.enable("false")) multiplexer_1 (
    .in0(multiplexer_2_out), .in1(not_1_out), .out(multiplexer_1_out), .sel(T));
  Multiplexer #(.enable("false")) multiplexer_2 (.in0(Q), .in1(D), .out(multiplexer_2_out), .sel(W));
  not not_1 (not_1_out, Q);
endmodule

module COUTER8 (
  input  I,
  input  [7:0] D,
  input  W,
  input  C,
  input  R,
  output [7:0] Q
);

  wire and_1_out, and_2_out, and_3_out, and_4_out, and_5_out, and_6_out, and_7_out;

  and and_1 (and_1_out, Q[0], I);
  TOGGLE toggle_1 (.C(C), .R(R), .T(and_1_out), .D(D[1]), .Q(Q[1]), .W(W));
  TOGGLE toggle_2 (.C(C), .R(R), .T(I), .D(D[0]), .Q(Q[0]), .W(W));
  and and_2 (and_2_out, and_1_out, Q[1]);
  TOGGLE toggle_3 (.C(C), .R(R), .T(and_2_out), .D(D[2]), .Q(Q[2]), .W(W));
  and and_3 (and_3_out, and_2_out, Q[2]);
  TOGGLE toggle_4 (.C(C), .R(R), .T(and_3_out), .D(D[3]), .Q(Q[3]), .W(W));
  and and_4 (and_4_out, and_3_out, Q[3]);
  and and_5 (and_5_out, and_4_out, Q[4]);
  TOGGLE toggle_5 (.C(C), .R(R), .T(and_5_out), .D(D[5]), .Q(Q[5]), .W(W));
  TOGGLE toggle_6 (.C(C), .R(R), .T(and_4_out), .D(D[4]), .Q(Q[4]), .W(W));
  and and_6 (and_6_out, and_5_out, Q[5]);
  TOGGLE toggle_7 (.C(C), .R(R), .T(and_6_out), .D(D[6]), .Q(Q[6]), .W(W));
  and and_7 (and_7_out, and_6_out, Q[6]);
  TOGGLE toggle_8 (.C(C), .R(R), .T(and_7_out), .D(D[7]), .Q(Q[7]), .W(W));

  // Notes on the sheet:
  //   0
  //   7
endmodule

module COUNTER2 (
  input  I,
  input  [1:0] D,
  input  W,
  input  C,
  input  R,
  output [1:0] Q
);

  wire and_1_out;

  and and_1 (and_1_out, Q[0], I);
  TOGGLE toggle_1 (.C(C), .R(R), .T(and_1_out), .D(D[1]), .Q(Q[1]), .W(W));
  TOGGLE toggle_2 (.C(C), .R(R), .T(I), .D(D[0]), .Q(Q[0]), .W(W));

  // Notes on the sheet:
  //   0
  //   1
endmodule
