// Logisim project CPU8_ONE_CYCLE_ARITH.circ as structural Verilog: 16 circuits, main circuit BOARD
module BOARD (
);

  wire and_1_out, and_2_out, and_3_out, and_4_out, and_5_out, and_6_out, and_7_out, and_8_out, and_9_out,
       and_10_out, and_11_out, and_12_out, and_13_out, and_14_out, and_15_out, and_16_out, and_17_out,
       and_18_out, and_19_out, and_20_out, and_21_out, and_22_out, and_23_out, and_24_out, and_25_out,
       CLOCK_out, controlled_buffer_26_out, dec4_1__0_2, dec4_1__1_2, dec4_1__2_2, dec4_1__3_2, dec4_1__4,
       dec4_1__5, dec4_1__6, dec4_1__7, dec4_1__8, dec4_1__9, dec4_1_a, dec4_1_b, dec4_1_c, dec4_1_d,
       dec4_1_e_2, dec4_1_f, decoder_1_out0, decoder_1_out1, decoder_1_out2, decoder_1_out3, decoder_2_out0,
       decoder_2_out1, decoder_2_out2, decoder_2_out3, decoder_2_out4, decoder_2_out5, decoder_2_out6,
       decoder_2_out7, multiplexer_4_out, multiplexer_6_out, not_1_out, not_2_out, not_3_out, not_4_out,
       not_5_out, not_6_out, or_1_out, or_2_out, or_3_out, or_4_out, or_5_out, pull_resistor_2_node,
       pull_resistor_10_node, pull_resistor_12_node, RESET_out, toggle_1_q, toggle_2_q, toggle_3_q;
  wire [0:0] controlled_buffer_10_out;
  wire [1:0] controlled_buffer_1_out, controlled_buffer_2_out, controlled_buffer_9_out,
       controlled_buffer_12_out, controlled_buffer_30_out, multiplexer_1_out_2;
  wire [2:0] controlled_buffer_8_out, controlled_buffer_15_out, controlled_buffer_16_out,
       controlled_buffer_19_out, controlled_buffer_20_out;
  wire [5:0] controlled_buffer_2_out_2;
  wire [7:0] A_2_q, alu_1_r, controlled_buffer_3_out, controlled_buffer_6_out, controlled_buffer_11_out,
       controlled_buffer_22_out, controlled_buffer_38_out, demultiplexer_1_out4, F_q, multiplexer_1_out,
       multiplexer_2_out, multiplexer_3_out, multiplexer_5_out, P_q, R_2_q, rom_1_data, W_q, X_q, Y_q, Z_q;

  Pull_Resistor pull_resistor_1 (.node(controlled_buffer_8_out[1]));
  Decoder #(.select(2), .disabled(0)) decoder_1 (
    .out0(decoder_1_out0), .out1(decoder_1_out1), .out2(decoder_1_out2), .out3(decoder_1_out3),
    .sel(controlled_buffer_9_out), .en(controlled_buffer_8_out[1]));
  TOGGLE toggle_1 (.C(or_1_out), .R(RESET_out), .T(1'b1), .D(1'b0), .Q(toggle_1_q), .W(1'b0));
  Counter counter_1 (.clk(decoder_1_out0), .clr(RESET_out));  // open: load, D, count, Q, carry
  TOGGLE toggle_2 (.C(and_1_out), .R(RESET_out), .T(1'b1), .D(1'b0), .Q(toggle_2_q), .W(1'b0));
  and and_1 (and_1_out, multiplexer_6_out, toggle_1_q, ~and_16_out, or_2_out);  // AND_Gate
  Multiplexer #(.width(8), .enable("false")) multiplexer_1 (
    .in0({controlled_buffer_2_out, controlled_buffer_2_out_2}), .in1(F_q),
    .out({multiplexer_1_out[7:6], multiplexer_1_out_2, multiplexer_1_out[3:0]}), .sel(multiplexer_6_out));
  not not_1 (not_1_out, multiplexer_6_out);
  Pull_Resistor pull_resistor_2 (.node(pull_resistor_2_node));
  or or_1 (or_1_out, and_7_out, and_8_out);
  or or_2 (or_2_out, and_6_out, and_2_out);
  and and_2 (and_2_out, ~toggle_2_q, ~multiplexer_1_out[1], multiplexer_1_out[0]);  // AND_Gate
  assign controlled_buffer_1_out = and_2_out ? 2'b11 : 2'bz;  // Controlled_Buffer controlled_buffer_1
  TOGGLE toggle_3 (.C(not_1_out), .R(or_3_out), .T(1'b1), .D(1'b0), .Q(toggle_3_q), .W(1'b0));
  or or_3 (or_3_out, RESET_out, and_3_out);
  and and_3 (and_3_out, ~multiplexer_6_out, toggle_3_q);  // AND_Gate
  and and_4 (and_4_out, decoder_1_out3, pull_resistor_2_node);
  assign {controlled_buffer_2_out, controlled_buffer_2_out_2} = and_4_out ? Z_q : 8'bz;  // Controlled_Buffer controlled_buffer_2
  assign controlled_buffer_3_out = not_2_out ? {controlled_buffer_2_out, controlled_buffer_2_out_2} : 8'bz;  // Controlled_Buffer controlled_buffer_3
  // Probe on Z_q
  REG8 Z (.C(and_5_out), ._0(RESET_out), .D(controlled_buffer_3_out), .Q(Z_q));
  and and_5 (and_5_out, decoder_1_out3, multiplexer_6_out);
  and and_6 (and_6_out, F_q[0], ~F_q[1], 1'b0);  // AND_Gate
  and and_7 (and_7_out, and_2_out, ~toggle_1_q);  // AND_Gate
  and and_8 (and_8_out, and_6_out, toggle_1_q);
  and and_9 (and_9_out, ~controlled_buffer_2_out_2[0], ~controlled_buffer_2_out_2[1], toggle_3_q, ~toggle_1_q);  // AND_Gate
  and and_10 (and_10_out, ~toggle_1_q, ~toggle_3_q, ~controlled_buffer_2_out_2[1], ~controlled_buffer_2_out_2[0]);  // AND_Gate
  assign controlled_buffer_12_out[1] = and_10_out ? 1'b0 : 1'bz;  // Controlled_Buffer controlled_buffer_4
  assign {controlled_buffer_2_out, controlled_buffer_2_out_2} = and_14_out ? Y_q : 8'bz;  // Controlled_Buffer controlled_buffer_5
  assign controlled_buffer_6_out = not_2_out ? {controlled_buffer_2_out, controlled_buffer_2_out_2} : 8'bz;  // Controlled_Buffer controlled_buffer_6
  // Probe on Y_q
  REG8 Y (.C(and_11_out), ._0(RESET_out), .D(controlled_buffer_6_out), .Q(Y_q));
  and and_11 (and_11_out, decoder_1_out2, multiplexer_6_out);
  assign {controlled_buffer_8_out[1], controlled_buffer_8_out[2]} = and_12_out ? 2'b11 : 2'bz;  // Controlled_Buffer controlled_buffer_7
  and and_12 (and_12_out, ~F_q[2], ~F_q[3], and_6_out);  // AND_Gate
  and and_13 (and_13_out, and_2_out, ~multiplexer_1_out[3], ~multiplexer_1_out[2]);  // AND_Gate
  assign {controlled_buffer_8_out[0], controlled_buffer_8_out[1], controlled_buffer_8_out[2]} = and_9_out ? 3'b111 : 3'bz;  // Controlled_Buffer controlled_buffer_8
  assign controlled_buffer_9_out = and_9_out ? controlled_buffer_2_out : 2'bz;  // Controlled_Buffer controlled_buffer_9
  assign {controlled_buffer_8_out[0], controlled_buffer_10_out[0]} = and_10_out ? 2'b11 : 2'bz;  // Controlled_Buffer controlled_buffer_10
  and and_14 (and_14_out, decoder_1_out2, pull_resistor_2_node);
  assign controlled_buffer_11_out = not_2_out ? {controlled_buffer_2_out, controlled_buffer_2_out_2} : 8'bz;  // Controlled_Buffer controlled_buffer_11
  REG8 X (.C(and_18_out), ._0(RESET_out), .D(controlled_buffer_11_out), .Q(X_q));
  assign {controlled_buffer_10_out[0], controlled_buffer_1_out[0], controlled_buffer_12_out} = and_12_out ? 4'b0000 : 4'bz;  // Controlled_Buffer controlled_buffer_12
  and and_15 (and_15_out, and_13_out, multiplexer_6_out);
  and and_16 (and_16_out, ~multiplexer_6_out, and_13_out);  // AND_Gate
  assign controlled_buffer_10_out[0] = and_16_out ? 1'b1 : 1'bz;  // Controlled_Buffer controlled_buffer_13
  assign controlled_buffer_12_out[1] = and_16_out ? 1'b0 : 1'bz;  // Controlled_Buffer controlled_buffer_14
  assign controlled_buffer_15_out = and_9_out ? {1'b0, controlled_buffer_2_out} : 3'bz;  // Controlled_Buffer controlled_buffer_15
  assign controlled_buffer_16_out = and_10_out ? controlled_buffer_2_out_2[4:2] : 3'bz;  // Controlled_Buffer controlled_buffer_16
  and and_17 (and_17_out, decoder_1_out1, pull_resistor_2_node);
  assign {controlled_buffer_2_out, controlled_buffer_2_out_2} = and_17_out ? X_q : 8'bz;  // Controlled_Buffer controlled_buffer_17
  // Probe on X_q
  and and_18 (and_18_out, decoder_1_out1, multiplexer_6_out);
  assign controlled_buffer_9_out = and_12_out ? F_q[5:4] : 2'bz;  // Controlled_Buffer controlled_buffer_18
  assign controlled_buffer_19_out = and_16_out ? {1'b0, multiplexer_1_out[7:6]} : 3'bz;  // Controlled_Buffer controlled_buffer_19
  and and_19 (and_19_out, and_10_out, ~controlled_buffer_2_out_2[5]);  // AND_Gate
  assign controlled_buffer_20_out = and_19_out ? 3'b000 : 3'bz;  // Controlled_Buffer controlled_buffer_20
  and and_20 (and_20_out, decoder_1_out0, pull_resistor_2_node);
  assign {controlled_buffer_2_out, controlled_buffer_2_out_2} = and_20_out ? W_q : 8'bz;  // Controlled_Buffer controlled_buffer_21
  assign controlled_buffer_22_out = not_2_out ? {controlled_buffer_2_out, controlled_buffer_2_out_2} : 8'bz;  // Controlled_Buffer controlled_buffer_22
  // Probe on W_q
  REG8 W (.C(and_21_out), ._0(RESET_out), .D(controlled_buffer_22_out), .Q(W_q));
  and and_21 (and_21_out, decoder_1_out0, multiplexer_6_out);
  and and_22 (and_22_out, F_q[2], ~F_q[3], and_6_out);  // AND_Gate
  assign controlled_buffer_16_out = and_16_out ? 3'b001 : 3'bz;  // Controlled_Buffer controlled_buffer_23
  assign controlled_buffer_20_out = and_16_out ? 3'b101 : 3'bz;  // Controlled_Buffer controlled_buffer_24
  assign controlled_buffer_19_out = and_19_out ? {1'b0, controlled_buffer_2_out} : 3'bz;  // Controlled_Buffer controlled_buffer_25
  // Probe on controlled_buffer_20_out
  Multiplexer #(.select(3), .width(8)) multiplexer_2 (
    .in0(W_q), .in1(X_q), .in2(Y_q), .in3(Z_q), .in4({controlled_buffer_2_out, controlled_buffer_2_out_2}),
    .in5({8{1'b0}}), .out(multiplexer_2_out), .sel(controlled_buffer_20_out), .en(controlled_buffer_10_out[0]));  // open: in6, in7
  Decoder #(.select(3), .enable("false")) decoder_2 (
    .out0(decoder_2_out0), .out1(decoder_2_out1), .out2(decoder_2_out2), .out3(decoder_2_out3),
    .out4(decoder_2_out4), .out5(decoder_2_out5), .out6(decoder_2_out6), .out7(decoder_2_out7),
    .sel(controlled_buffer_16_out));
  assign controlled_buffer_26_out = and_22_out ? 1'b1 : 1'bz;  // Controlled_Buffer controlled_buffer_26
  assign controlled_buffer_9_out = and_15_out ? multiplexer_1_out_2 : 2'bz;  // Controlled_Buffer controlled_buffer_27
  and and_23 (and_23_out, and_10_out, controlled_buffer_2_out_2[5]);
  assign controlled_buffer_19_out = and_23_out ? 3'b000 : 3'bz;  // Controlled_Buffer controlled_buffer_28
  Pull_Resistor pull_resistor_3 (.node(controlled_buffer_8_out[2]));
  Pull_Resistor pull_resistor_4 (.node(controlled_buffer_10_out[0]));
  // Probe on controlled_buffer_19_out
  not not_2 (not_2_out, controlled_buffer_8_out[2]);
  Multiplexer #(.select(3), .width(8)) multiplexer_3 (
    .in0(W_q), .in1(X_q), .in2(Y_q), .in3(Z_q), .in4({controlled_buffer_2_out, controlled_buffer_2_out_2}),
    .in5({8{1'b0}}), .out(multiplexer_3_out), .sel(controlled_buffer_19_out), .en(controlled_buffer_10_out[0]));  // open: in6, in7
  assign controlled_buffer_8_out[1] = and_22_out ? 1'b1 : 1'bz;  // Controlled_Buffer controlled_buffer_29
  assign controlled_buffer_30_out = and_22_out ? 2'b00 : 2'bz;  // Controlled_Buffer controlled_buffer_30
  assign controlled_buffer_8_out = and_15_out ? 3'b111 : 3'bz;  // Controlled_Buffer controlled_buffer_31
  assign controlled_buffer_15_out = and_15_out ? {1'b0, multiplexer_1_out_2} : 3'bz;  // Controlled_Buffer controlled_buffer_32
  assign controlled_buffer_20_out = and_23_out ? {1'b0, controlled_buffer_2_out} : 3'bz;  // Controlled_Buffer controlled_buffer_33
  // Probe on controlled_buffer_15_out
  Demultiplexer #(.select(3), .width(8)) demultiplexer_1 (
    .out0(controlled_buffer_22_out), .out1(controlled_buffer_11_out), .out2(controlled_buffer_6_out),
    .out3(controlled_buffer_3_out), .out4(demultiplexer_1_out4), .in(R_2_q), .sel(controlled_buffer_15_out),
    .en(controlled_buffer_8_out[2]));  // open: out5, out6, out7
  // Probe on alu_1_r
  ALU alu_1 (
    .LSR(decoder_2_out6), .LSL(decoder_2_out7), .NOT(decoder_2_out3), .OR(decoder_2_out4),
    .AND(decoder_2_out5), .ADD(decoder_2_out1), .SUB(decoder_2_out2), .A(multiplexer_3_out),
    .B(multiplexer_2_out), .R(alu_1_r), .INC(decoder_2_out0));  // open: C
  assign controlled_buffer_9_out = and_22_out ? F_q[5:4] : 2'bz;  // Controlled_Buffer controlled_buffer_34
  // Probe on R_2_q
  REG8 R_2 (.C(not_3_out), ._0(RESET_out), .D(alu_1_r), .Q(R_2_q));
  not not_3 (not_3_out, multiplexer_6_out);
  assign controlled_buffer_1_out[1] = and_22_out ? 1'b1 : 1'bz;  // Controlled_Buffer controlled_buffer_35
  Pull_Resistor #(.pull(1)) pull_resistor_5 (.node(controlled_buffer_30_out[1]));
  Pull_Resistor pull_resistor_6 (.node(controlled_buffer_1_out[1]));
  Pull_Resistor pull_resistor_7 (.node(controlled_buffer_8_out[0]));
  Pull_Resistor pull_resistor_8 (.node(controlled_buffer_26_out));
  // Probe on A_2_q
  REG8 A_2 (.C(and_24_out), ._0(RESET_out), .D({controlled_buffer_2_out, controlled_buffer_2_out_2}), .Q(A_2_q));
  and and_24 (and_24_out, controlled_buffer_30_out[1], multiplexer_6_out);
  not not_4 (not_4_out, multiplexer_6_out);
  Pull_Resistor #(.pull(1)) pull_resistor_9 (.node(controlled_buffer_1_out[0]));
  Pull_Resistor pull_resistor_10 (.node(pull_resistor_10_node));
  Pull_Resistor #(.pull(1)) pull_resistor_11 (.node(controlled_buffer_12_out[1]));
  Pull_Resistor #(.pull(1)) pull_resistor_12 (.node(pull_resistor_12_node));
  REG8 F (.C(or_4_out), ._0(RESET_out), .D({controlled_buffer_2_out, controlled_buffer_2_out_2}), .Q(F_q));
  Multiplexer #(.enable("false")) multiplexer_4 (
    .in0(not_4_out), .in1(multiplexer_6_out), .out(multiplexer_4_out), .sel(controlled_buffer_8_out[0]));
  Pull_Resistor #(.pull(1)) pull_resistor_13 (.node(controlled_buffer_12_out[0]));
  COUTER8 P (
    .I(controlled_buffer_12_out[1]), .D({controlled_buffer_2_out, controlled_buffer_2_out_2}),
    .W(pull_resistor_10_node), .C(multiplexer_4_out), .R(RESET_out), .Q(P_q));
  // Probe on P_q
  assign {controlled_buffer_2_out, controlled_buffer_2_out_2} = not_5_out ? rom_1_data : 8'bz;  // Controlled_Buffer controlled_buffer_36
  // Probe on {controlled_buffer_2_out, controlled_buffer_2_out_2}
  // Probe on F_q
  or or_4 (or_4_out, controlled_buffer_1_out[1], and_25_out);
  and and_25 (and_25_out, controlled_buffer_1_out[0], multiplexer_4_out);
  not not_5 (not_5_out, or_5_out);
  assign {controlled_buffer_2_out, controlled_buffer_2_out_2} = or_5_out ? {8{1'b1}} : 8'bz;  // Controlled_Buffer controlled_buffer_37
  Multiplexer #(.width(8), .enable("false")) multiplexer_5 (
    .in0(P_q), .in1(A_2_q), .out(multiplexer_5_out), .sel(controlled_buffer_26_out));
  not not_6 (not_6_out, pull_resistor_12_node);
  assign controlled_buffer_38_out = not_6_out ? {controlled_buffer_2_out, controlled_buffer_2_out_2} : 8'bz;  // Controlled_Buffer controlled_buffer_38
  Multiplexer #(.enable("false")) multiplexer_6 (.in0(CLOCK_out), .in1(1'b0), .out(multiplexer_6_out), .sel(or_5_out));
  DEC4 dec4_1 (
    ._0(multiplexer_5_out[4]), ._1(multiplexer_5_out[5]), ._2(multiplexer_5_out[6]),
    ._3(multiplexer_5_out[7]), ._0_2(dec4_1__0_2), ._1_2(dec4_1__1_2), ._2_2(dec4_1__2_2),
    ._3_2(dec4_1__3_2), ._4(dec4_1__4), ._5(dec4_1__5), ._6(dec4_1__6), ._7(dec4_1__7), ._8(dec4_1__8),
    ._9(dec4_1__9), .A(dec4_1_a), .B(dec4_1_b), .C(dec4_1_c), .D(dec4_1_d), .E_2(dec4_1_e_2), .F(dec4_1_f),
    .E(controlled_buffer_12_out[0]));
  LED HALT (.in(or_5_out));
  ROM #(.addrWidth(4)) rom_1 (.addr(multiplexer_5_out[3:0]), .data(rom_1_data), .sel(dec4_1__0_2));
  or or_5 (or_5_out, dec4_1__7, dec4_1__1_2, dec4_1__2_2, dec4_1__3_2, dec4_1__4, dec4_1__5, dec4_1__6, dec4_1__8, dec4_1__9, dec4_1_a, dec4_1_b, dec4_1_c, dec4_1_d, dec4_1_e_2);
  RAM16 ram16_1 (
    .SELECT(dec4_1_f), .CLOCK(multiplexer_6_out), .READ(pull_resistor_12_node), .RESET(RESET_out),
    .ADDRESS(multiplexer_5_out[3:0]), .IN(controlled_buffer_38_out), .OUT(rom_1_data));
  Button RESET (.out(RESET_out));
  Clock CLOCK (.out(CLOCK_out));

  // Notes on the sheet:
  //   D-BUS
  //   P2
  //   P1
  //   RR
  //   RR
  //   P2
  //   P1
  //   DST
  //   DST
  //   ARITHMETIC
  //   OP
  //   DST
  //   SRC
  //   SRC
  //   DIR
  //   RM
  //   DST
  //   DST
  //   DST
  //   DST
  //   SRC
  //   C-BUS
  //   MOVES
  //   contents of rom_1 (hex, n*v repeats v):
  //   0 11 c4
  //   NON-EXISTING
  //   ADDRESSES
endmodule

module ALU (
  input  LSR,
  input  LSL,
  input  NOT,
  input  OR,
  input  AND,
  input  ADD,
  input  SUB,
  input  INC,
  input  [7:0] A,
  input  [7:0] B,
  output [7:0] R,
  output C
);

  wire or_2_out, or_3_out;
  wire [7:0] add8_1_r, and_1_out, bit_extender_1_out, lsl_1_o, lsr_1_o, multiplexer_1_out, not_1_out,
       or_1_out, xor_1_out;

  Multiplexer #(.width(8), .enable("false")) multiplexer_1 (.in0(B), .in1(8'h1), .out(multiplexer_1_out), .sel(INC));
  // Probe on multiplexer_1_out
  LSR lsr_1 (.I(A), .O(lsr_1_o));
  LSL lsl_1 (.O(lsl_1_o), .I(A));
  assign R = LSR ? lsr_1_o : 8'bz;  // Controlled_Buffer controlled_buffer_1
  assign R = LSL ? lsl_1_o : 8'bz;  // Controlled_Buffer controlled_buffer_2
  assign R = NOT ? not_1_out : 8'bz;  // Controlled_Buffer controlled_buffer_3
  assign not_1_out = ~A;  // NOT_Gate not_1, 8 bits wide
  assign R = OR ? or_1_out : 8'bz;  // Controlled_Buffer controlled_buffer_4
  assign or_1_out = A | multiplexer_1_out;  // OR_Gate or_1, 8 bits wide
  assign and_1_out = A & multiplexer_1_out;  // AND_Gate and_1, 8 bits wide
  assign R = AND ? and_1_out : 8'bz;  // Controlled_Buffer controlled_buffer_5
  assign bit_extender_1_out = {{7{SUB}}, SUB};  // Bit_Extender bit_extender_1
  assign xor_1_out = multiplexer_1_out ^ bit_extender_1_out;  // XOR_Gate xor_1, 8 bits wide
  or or_2 (or_2_out, ADD, SUB);
  or or_3 (or_3_out, INC, or_2_out);
  ADD8 add8_1 (.C(SUB), .A(A), .B(xor_1_out), .R(add8_1_r), .C_2(C));
  assign R = or_3_out ? add8_1_r : 8'bz;  // Controlled_Buffer controlled_buffer_6
endmodule

module ADD1 (
  input  Ci,
  input  A,
  input  B,
  output R,
  output Co
);

  wire and_1_out, and_2_out, xor_1_out;

  and and_1 (and_1_out, A, B);
  xor xor_1 (xor_1_out, A, B);
  xor xor_2 (R, Ci, xor_1_out);
  and and_2 (and_2_out, Ci, xor_1_out);
  or or_1 (Co, and_2_out, and_1_out);
endmodule

module ADD8 (
  input  C,
  input  [7:0] A,
  input  [7:0] B,
  output [7:0] R,
  output C_2
);

  wire add1_1_co, add1_2_co, add1_3_co, add1_4_co, add1_5_co, add1_6_co, add1_7_co;

  ADD1 add1_1 (.A(A[0]), .B(B[0]), .R(R[0]), .Ci(C), .Co(add1_1_co));
  ADD1 add1_2 (.A(A[1]), .B(B[1]), .R(R[1]), .Ci(add1_1_co), .Co(add1_2_co));
  ADD1 add1_3 (.A(A[2]), .B(B[2]), .R(R[2]), .Ci(add1_2_co), .Co(add1_3_co));
  ADD1 add1_4 (.A(A[3]), .B(B[3]), .R(R[3]), .Ci(add1_3_co), .Co(add1_4_co));
  ADD1 add1_5 (.A(A[4]), .B(B[4]), .R(R[4]), .Ci(add1_4_co), .Co(add1_5_co));
  ADD1 add1_6 (.A(A[5]), .B(B[5]), .R(R[5]), .Ci(add1_5_co), .Co(add1_6_co));
  ADD1 add1_7 (.A(A[6]), .B(B[6]), .R(R[6]), .Ci(add1_6_co), .Co(add1_7_co));
  ADD1 add1_8 (.A(A[7]), .B(B[7]), .R(R[7]), .Ci(add1_7_co), .Co(C_2));
endmodule

module LSL (
  input  [7:0] I,
  output [7:0] O
);


  assign O = {I[6:0], 1'b0};
endmodule

module LSR (
  input  [7:0] I,
  output [7:0] O
);


  assign O = {1'b0, I[7:1]};
endmodule

module SR_LATCH (
  input  S,
  input  E,
  input  R,
  output Q
);

  wire and_1_out, and_2_out, nor_1_out;

  and and_1 (and_1_out, S, E);
  and and_2 (and_2_out, E, R);
  nor nor_1 (nor_1_out, and_1_out, Q);
  nor nor_2 (Q, nor_1_out, and_2_out);
endmodule

module D_LATCH (
  input  D,
  input  E,
  input  _0,
  output Q
);

  wire and_1_out, and_2_out, nor_1_out, or_1_out;

  and and_1 (and_1_out, D, E);
  and and_2 (and_2_out, E, ~D);  // AND_Gate
  or or_1 (or_1_out, and_2_out, _0);
  nor nor_1 (nor_1_out, and_1_out, Q);
  nor nor_2 (Q, nor_1_out, or_1_out);
endmodule

module D_FLIP_FLOP (
  input  D,
  input  C,
  input  R,
  output Q
);

  wire and_1_out, and_2_out, and_3_out, and_4_out, nor_1_out, nor_2_out, nor_3_out, not_1_out, or_1_out,
       or_2_out;

  and and_1 (and_1_out, D, C);
  and and_2 (and_2_out, C, ~D);  // AND_Gate
  nor nor_1 (nor_1_out, and_1_out, nor_2_out);
  nor nor_2 (nor_2_out, nor_1_out, or_1_out);
  or or_1 (or_1_out, and_2_out, R);
  not not_1 (not_1_out, C);
  and and_3 (and_3_out, nor_2_out, not_1_out);
  and and_4 (and_4_out, not_1_out, ~nor_2_out);  // AND_Gate
  nor nor_3 (nor_3_out, and_3_out, Q);
  nor nor_4 (Q, nor_3_out, or_2_out);
  or or_2 (or_2_out, and_4_out, R);
endmodule

module REG8 (
  input  C,
  input  _0,
  input  [7:0] D,
  output [7:0] Q
);

  D_FLIP_FLOP d_flip_flop_1 (.D(D[6]), .C(C), .R(_0), .Q(Q[6]));
  D_FLIP_FLOP d_flip_flop_2 (.D(D[7]), .C(C), .R(_0), .Q(Q[7]));
  D_FLIP_FLOP d_flip_flop_3 (.D(D[5]), .C(C), .R(_0), .Q(Q[5]));
  D_FLIP_FLOP d_flip_flop_4 (.D(D[4]), .C(C), .R(_0), .Q(Q[4]));
  D_FLIP_FLOP d_flip_flop_5 (.D(D[3]), .C(C), .R(_0), .Q(Q[3]));
  D_FLIP_FLOP d_flip_flop_6 (.D(D[2]), .C(C), .R(_0), .Q(Q[2]));
  D_FLIP_FLOP d_flip_flop_7 (.D(D[0]), .C(C), .R(_0), .Q(Q[0]));
  D_FLIP_FLOP d_flip_flop_8 (.D(D[1]), .C(C), .R(_0), .Q(Q[1]));

  // Notes on the sheet:
  //   7
  //   0
endmodule

module RAM16 (
  input  SELECT,
  input  CLOCK,
  input  READ,
  input  RESET,
  input  [3:0] ADDRESS,
  input  [7:0] IN,
  output [7:0] OUT
);

  wire and_1_out, and_2_out, and_3_out, and_4_out, and_5_out, and_6_out, and_7_out, and_8_out, and_9_out,
       and_10_out, and_11_out, and_12_out, and_13_out, and_14_out, and_15_out, and_16_out, and_17_out,
       and_18_out, and_19_out, and_20_out, and_21_out, and_22_out, and_23_out, and_24_out, and_25_out,
       and_26_out, and_27_out, and_28_out, and_29_out, and_30_out, and_31_out, and_32_out, dec4_1__0_2,
       dec4_1__1_2, dec4_1__2_2, dec4_1__3_2, dec4_1__4, dec4_1__5, dec4_1__6, dec4_1__7, dec4_1__8,
       dec4_1__9, dec4_1_a, dec4_1_b, dec4_1_c, dec4_1_d, dec4_1_e_2, dec4_1_f;
  wire [7:0] reg8_1_q, reg8_2_q, reg8_3_q, reg8_4_q, reg8_5_q, reg8_6_q, reg8_7_q, reg8_8_q, reg8_9_q,
       reg8_10_q, reg8_11_q, reg8_12_q, reg8_13_q, reg8_14_q, reg8_15_q, reg8_16_q;

  REG8 reg8_1 (.C(and_1_out), ._0(RESET), .D(IN), .Q(reg8_1_q));
  and and_1 (and_1_out, dec4_1_f, CLOCK);
  REG8 reg8_2 (.C(and_2_out), ._0(RESET), .D(IN), .Q(reg8_2_q));
  and and_2 (and_2_out, dec4_1_e_2, CLOCK);
  REG8 reg8_3 (.C(and_3_out), ._0(RESET), .D(IN), .Q(reg8_3_q));
  and and_3 (and_3_out, dec4_1_d, CLOCK);
  REG8 reg8_4 (.C(and_4_out), ._0(RESET), .D(IN), .Q(reg8_4_q));
  and and_4 (and_4_out, dec4_1_c, CLOCK);
  REG8 reg8_5 (.C(and_5_out), ._0(RESET), .D(IN), .Q(reg8_5_q));
  and and_5 (and_5_out, dec4_1_b, CLOCK);
  REG8 reg8_6 (.C(and_6_out), ._0(RESET), .D(IN), .Q(reg8_6_q));
  and and_6 (and_6_out, dec4_1_a, CLOCK);
  REG8 reg8_7 (.C(and_7_out), ._0(RESET), .D(IN), .Q(reg8_7_q));
  and and_7 (and_7_out, dec4_1__9, CLOCK);
  REG8 reg8_8 (.C(and_8_out), ._0(RESET), .D(IN), .Q(reg8_8_q));
  and and_8 (and_8_out, dec4_1__8, CLOCK);
  DEC4 dec4_1 (
    ._0(ADDRESS[0]), ._1(ADDRESS[1]), ._2(ADDRESS[2]), ._3(ADDRESS[3]), ._0_2(dec4_1__0_2),
    ._1_2(dec4_1__1_2), ._2_2(dec4_1__2_2), ._3_2(dec4_1__3_2), ._4(dec4_1__4), ._5(dec4_1__5),
    ._6(dec4_1__6), ._7(dec4_1__7), ._8(dec4_1__8), ._9(dec4_1__9), .A(dec4_1_a), .B(dec4_1_b), .C(dec4_1_c),
    .D(dec4_1_d), .E_2(dec4_1_e_2), .F(dec4_1_f), .E(SELECT));
  assign OUT = and_9_out ? reg8_1_q : 8'bz;  // Controlled_Buffer controlled_buffer_1
  and and_9 (and_9_out, dec4_1_f, READ);
  assign OUT = and_10_out ? reg8_2_q : 8'bz;  // Controlled_Buffer controlled_buffer_2
  and and_10 (and_10_out, dec4_1_e_2, READ);
  assign OUT = and_11_out ? reg8_3_q : 8'bz;  // Controlled_Buffer controlled_buffer_3
  and and_11 (and_11_out, dec4_1_d, READ);
  assign OUT = and_12_out ? reg8_4_q : 8'bz;  // Controlled_Buffer controlled_buffer_4
  and and_12 (and_12_out, dec4_1_c, READ);
  assign OUT = and_13_out ? reg8_5_q : 8'bz;  // Controlled_Buffer controlled_buffer_5
  and and_13 (and_13_out, dec4_1_b, READ);
  assign OUT = and_14_out ? reg8_6_q : 8'bz;  // Controlled_Buffer controlled_buffer_6
  and and_14 (and_14_out, dec4_1_a, READ);
  assign OUT = and_15_out ? reg8_7_q : 8'bz;  // Controlled_Buffer controlled_buffer_7
  and and_15 (and_15_out, dec4_1__9, READ);
  assign OUT = and_16_out ? reg8_8_q : 8'bz;  // Controlled_Buffer controlled_buffer_8
  and and_16 (and_16_out, dec4_1__8, READ);
  and and_17 (and_17_out, dec4_1__0_2, READ);
  assign OUT = and_17_out ? reg8_9_q : 8'bz;  // Controlled_Buffer controlled_buffer_9
  and and_18 (and_18_out, dec4_1__1_2, READ);
  assign OUT = and_18_out ? reg8_10_q : 8'bz;  // Controlled_Buffer controlled_buffer_10
  and and_19 (and_19_out, dec4_1__2_2, READ);
  assign OUT = and_19_out ? reg8_11_q : 8'bz;  // Controlled_Buffer controlled_buffer_11
  and and_20 (and_20_out, dec4_1__3_2, READ);
  assign OUT = and_20_out ? reg8_12_q : 8'bz;  // Controlled_Buffer controlled_buffer_12
  and and_21 (and_21_out, dec4_1__4, READ);
  assign OUT = and_21_out ? reg8_13_q : 8'bz;  // Controlled_Buffer controlled_buffer_13
  and and_22 (and_22_out, dec4_1__5, READ);
  assign OUT = and_22_out ? reg8_14_q : 8'bz;  // Controlled_Buffer controlled_buffer_14
  and and_23 (and_23_out, dec4_1__6, READ);
  assign OUT = and_23_out ? reg8_15_q : 8'bz;  // Controlled_Buffer controlled_buffer_15
  and and_24 (and_24_out, dec4_1__7, READ);
  assign OUT = and_24_out ? reg8_16_q : 8'bz;  // Controlled_Buffer controlled_buffer_16
  REG8 reg8_9 (.C(and_25_out), ._0(RESET), .D(IN), .Q(reg8_9_q));
  REG8 reg8_10 (.C(and_26_out), ._0(RESET), .D(IN), .Q(reg8_10_q));
  REG8 reg8_11 (.C(and_27_out), ._0(RESET), .D(IN), .Q(reg8_11_q));
  REG8 reg8_12 (.C(and_28_out), ._0(RESET), .D(IN), .Q(reg8_12_q));
  REG8 reg8_13 (.C(and_29_out), ._0(RESET), .D(IN), .Q(reg8_13_q));
  REG8 reg8_14 (.C(and_30_out), ._0(RESET), .D(IN), .Q(reg8_14_q));
  REG8 reg8_15 (.C(and_31_out), ._0(RESET), .D(IN), .Q(reg8_15_q));
  REG8 reg8_16 (.C(and_32_out), ._0(RESET), .D(IN), .Q(reg8_16_q));
  and and_25 (and_25_out, dec4_1__0_2, CLOCK);
  and and_26 (and_26_out, dec4_1__1_2, CLOCK);
  and and_27 (and_27_out, dec4_1__2_2, CLOCK);
  and and_28 (and_28_out, dec4_1__3_2, CLOCK);
  and and_29 (and_29_out, dec4_1__4, CLOCK);
  and and_30 (and_30_out, dec4_1__5, CLOCK);
  and and_31 (and_31_out, dec4_1__6, CLOCK);
  and and_32 (and_32_out, dec4_1__7, CLOCK);

  // Notes on the sheet:
  //   OUT
  //   IN
endmodule

module DEC2 (
  input  _0,
  input  _1,
  input  E,
  output out_4,
  output out_5,
  output out_6,
  output out_7
);

  and and_1 (out_4, ~_0, ~_1, E);  // AND_Gate
  and and_2 (out_5, _0, ~_1, E);  // AND_Gate
  and and_3 (out_6, ~_0, _1, E);  // AND_Gate
  and and_4 (out_7, _0, _1, E);
endmodule

module DEC4 (
  input  _0,
  input  _1,
  input  _2,
  input  _3,
  input  E,
  output _0_2,
  output _1_2,
  output _2_2,
  output _3_2,
  output _4,
  output _5,
  output _6,
  output _7,
  output _8,
  output _9,
  output A,
  output B,
  output C,
  output D,
  output E_2,
  output F
);

  wire dec2_1_out_4, dec2_1_out_5, dec2_1_out_6, dec2_1_out_7;

  DEC2 dec2_1 (
    ._0(_2), ._1(_3), .out_4(dec2_1_out_4), .out_5(dec2_1_out_5), .out_6(dec2_1_out_6), .out_7(dec2_1_out_7),
    .E(E));
  DEC2 dec2_2 (._0(_0), ._1(_1), .out_4(_0_2), .out_5(_1_2), .out_6(_2_2), .out_7(_3_2), .E(dec2_1_out_4));
  DEC2 dec2_3 (._0(_0), ._1(_1), .out_4(_4), .out_5(_5), .out_6(_6), .out_7(_7), .E(dec2_1_out_5));
  DEC2 dec2_4 (._0(_0), ._1(_1), .out_4(_8), .out_5(_9), .out_6(A), .out_7(B), .E(dec2_1_out_6));
  DEC2 dec2_5 (._0(_0), ._1(_1), .out_4(C), .out_5(D), .out_6(E_2), .out_7(F), .E(dec2_1_out_7));
endmodule

module TOGGLE (
  input  C,
  input  R,
  input  T,
  input  W,
  input  D,
  output Q
);

  wire multiplexer_1_out, multiplexer_2_out, not_1_out;

  D_FLIP_FLOP d_flip_flop_1 (.D(multiplexer_1_out), .C(C), .R(R), .Q(Q));
  Multiplexer #(.enable("false")) multiplexer_1 (
    .in0(multiplexer_2_out), .in1(not_1_out), .out(multiplexer_1_out), .sel(T));
  not not_1 (not_1_out, Q);
  Multiplexer #(.enable("false")) multiplexer_2 (.in0(Q), .in1(D), .out(multiplexer_2_out), .sel(W));
endmodule

module COUTER8 (
  input  I,
  input  [7:0] D,
  input  W,
  input  C,
  input  R,
  output [7:0] Q
);

  wire and_1_out, and_2_out, and_3_out, and_4_out, and_5_out, and_6_out, and_7_out;

  and and_1 (and_1_out, Q[0], I);
  TOGGLE toggle_1 (.C(C), .R(R), .T(and_1_out), .D(D[1]), .Q(Q[1]), .W(W));
  TOGGLE toggle_2 (.C(C), .R(R), .T(I), .D(D[0]), .Q(Q[0]), .W(W));
  and and_2 (and_2_out, and_1_out, Q[1]);
  TOGGLE toggle_3 (.C(C), .R(R), .T(and_2_out), .D(D[2]), .Q(Q[2]), .W(W));
  and and_3 (and_3_out, and_2_out, Q[2]);
  TOGGLE toggle_4 (.C(C), .R(R), .T(and_3_out), .D(D[3]), .Q(Q[3]), .W(W));
  and and_4 (and_4_out, and_3_out, Q[3]);
  and and_5 (and_5_out, and_4_out, Q[4]);
  TOGGLE toggle_5 (.C(C), .R(R), .T(and_4_out), .D(D[4]), .Q(Q[4]), .W(W));
  TOGGLE toggle_6 (.C(C), .R(R), .T(and_5_out), .D(D[5]), .Q(Q[5]), .W(W));
  and and_6 (and_6_out, and_5_out, Q[5]);
  TOGGLE toggle_7 (.C(C), .R(R), .T(and_6_out), .D(D[6]), .Q(Q[6]), .W(W));
  and and_7 (and_7_out, and_6_out, Q[6]);
  TOGGLE toggle_8 (.C(C), .R(R), .T(and_7_out), .D(D[7]), .Q(Q[7]), .W(W));

  // Notes on the sheet:
  //   0
  //   7
endmodule

module COUNTER2 (
  input  I,
  input  [1:0] D,
  input  W,
  input  C,
  input  R,
  output [1:0] Q
);

  wire and_1_out;

  and and_1 (and_1_out, Q[0], I);
  TOGGLE toggle_1 (.C(C), .R(R), .T(and_1_out), .D(D[1]), .Q(Q[1]), .W(W));
  TOGGLE toggle_2 (.C(C), .R(R), .T(I), .D(D[0]), .Q(Q[0]), .W(W));

  // Notes on the sheet:
  //   0
  //   1
endmodule
